// Logisim project schematic.circ as structural Verilog: 56 circuits, main circuit main
module main (
  input  in_1,
  input  in_2,
  input  in_3,
  input  in_4,
  input  in_5,
  input  in_6,
  input  [3:0] in_7,
  input  in_8
);

  wire alu_1__16, alu_1_c, alu_1_n, alu_1_v, alu_1_z, alu_carry_1_co, clock_1_out, clock_2_out,
       ctrl_ram_1_nbuf, ctrl_ram_1_nce, ctrl_ram_1_nde, ctrl_ram_1_noe, ctrl_ram_1_nwe, not_1_out;
  wire [3:0] alu_16_bit_simple_1_f, alu_16_bit_simple_1_f_2, alu_16_bit_simple_1_f_3, alu_16_bit_simple_1_f_4;
  wire [7:0] ram_1_dout, ram_2_dout;

  DotMatrix #(.matrixcols(16), .matrixrows(1), .dotshape("circle")) dotmatrix_1 (
    .col0(1'b0), .col1(1'b1), .col2(1'b1), .col3(1'b1), .col4(1'b1), .col5(1'b1), .col6(1'b1), .col7(1'b1),
    .col8(1'b1), .col9(1'b1), .col10(1'b1), .col11(1'b1), .col12(1'b1), .col13(1'b1), .col14(1'b1),
    .col15(1'b1));
  DotMatrix #(.matrixcols(16), .matrixrows(1), .dotshape("circle")) dotmatrix_2 (
    .col0(1'b0), .col1(1'b0), .col2(1'b0), .col3(1'b0), .col4(1'b0), .col5(1'b0), .col6(1'b0), .col7(1'b0),
    .col8(1'b0), .col9(1'b0), .col10(1'b0), .col11(1'b0), .col12(1'b0), .col13(1'b0), .col14(1'b0),
    .col15(1'b1));
  DotMatrix #(.matrixcols(16), .matrixrows(1), .dotshape("circle")) dotmatrix_3 (
    .col0(alu_16_bit_simple_1_f_4[3]), .col1(alu_16_bit_simple_1_f_4[2]), .col2(alu_16_bit_simple_1_f_4[1]),
    .col3(alu_16_bit_simple_1_f_4[0]), .col4(alu_16_bit_simple_1_f_3[3]), .col5(alu_16_bit_simple_1_f_3[2]),
    .col6(alu_16_bit_simple_1_f_3[1]), .col7(alu_16_bit_simple_1_f_3[0]), .col8(alu_16_bit_simple_1_f_2[3]),
    .col9(alu_16_bit_simple_1_f_2[2]), .col10(alu_16_bit_simple_1_f_2[1]),
    .col11(alu_16_bit_simple_1_f_2[0]), .col12(alu_16_bit_simple_1_f[3]), .col13(alu_16_bit_simple_1_f[2]),
    .col14(alu_16_bit_simple_1_f[1]), .col15(alu_16_bit_simple_1_f[0]));
  Hex_Digit_Display hex_digit_display_1 (.value(4'b0111));  // open: dp
  Hex_Digit_Display hex_digit_display_2 (.value(4'b0000));  // open: dp
  Hex_Digit_Display hex_digit_display_3 (.value(alu_16_bit_simple_1_f_4));  // open: dp
  Hex_Digit_Display hex_digit_display_4 (.value(4'b1111));  // open: dp
  Hex_Digit_Display hex_digit_display_5 (.value(4'b1111));  // open: dp
  Hex_Digit_Display hex_digit_display_6 (.value(4'b0000));  // open: dp
  Hex_Digit_Display hex_digit_display_7 (.value(4'b0000));  // open: dp
  Hex_Digit_Display hex_digit_display_8 (.value(alu_16_bit_simple_1_f_2));  // open: dp
  Hex_Digit_Display hex_digit_display_9 (.value(alu_16_bit_simple_1_f_3));  // open: dp
  Hex_Digit_Display hex_digit_display_10 (.value(4'b1111));  // open: dp
  Hex_Digit_Display hex_digit_display_11 (.value(4'b0001));  // open: dp
  Hex_Digit_Display hex_digit_display_12 (.value(alu_16_bit_simple_1_f));  // open: dp
  ram ram_1 (.A({16{1'b0}}), .nCE(1'b0), .nWE(1'b1), .nOE(1'b1), .DIN(ram_1_dout), .DOUT(ram_1_dout));
  LED led_1 (.in(alu_1_c));
  DotMatrix #(.matrixcols(8), .matrixrows(1), .dotshape("circle")) dotmatrix_4 (
    .col0(ram_1_dout[7]), .col1(ram_1_dout[6]), .col2(ram_1_dout[5]), .col3(ram_1_dout[4]),
    .col4(ram_1_dout[3]), .col5(ram_1_dout[2]), .col6(ram_1_dout[1]), .col7(ram_1_dout[0]));
  Clock clock_1 (.out(clock_1_out));
  Clock clock_2 (.out(clock_2_out));
  assign ram_1_dout = 1'b0 ? {8{1'b0}} : 8'bz;  // Controlled_Buffer controlled_buffer_1
  ctrl_ram ctrl_ram_1 (
    .nCE(ctrl_ram_1_nce), .nBUF(ctrl_ram_1_nbuf), .nWE(ctrl_ram_1_nwe), .nOE(ctrl_ram_1_noe),
    .nDE(ctrl_ram_1_nde), .CLK(clock_2_out), .WR(in_1), .RD(in_3), .nRESET(in_2));  // open: nAE
  alu alu_1 (
    .C(alu_1_c), .Z(alu_1_z), .N(alu_1_n), .V(alu_1_v), .X(1'b1), .O0(1'b0), .O1(1'b0), .M(1'b0), .T(1'b1),
    .A(16'h7fff), .B(16'h1), .CLK(clock_1_out), ._16(alu_1__16));  // open: O
  ram ram_2 (
    .A(16'h2), .nCE(ctrl_ram_1_nce), .nWE(ctrl_ram_1_nwe), .nOE(ctrl_ram_1_noe), .DIN(ram_2_dout),
    .DOUT(ram_2_dout));
  alu_16_bit_simple alu_16_bit_simple_1 (
    .M(in_8), .S(in_7), .Cin(alu_carry_1_co), .A(16'h7fff), .B(16'h1),
    .F({alu_16_bit_simple_1_f_4, alu_16_bit_simple_1_f_3, alu_16_bit_simple_1_f_2, alu_16_bit_simple_1_f}));  // open: Co16, Co8
  not not_1 (not_1_out, ctrl_ram_1_nbuf);
  assign ram_2_dout = not_1_out ? 8'h67 : 8'bz;  // Controlled_Buffer controlled_buffer_2
  alu_carry alu_carry_1 (.Cin(in_4), .C(in_5), .N(in_6), .Co(alu_carry_1_co));
  Register register_1 (.D(ram_2_dout), .en(ctrl_ram_1_nde), .clk(clock_2_out));  // open: Q, clr
endmodule

module whole_cpu (
  input  nIRQ,
  input  [1:0] IRQN,
  input  nRESET,
  output [2:0] S,
  output [4:0] OPCODE,
  output [2:0] CTR,
  output [2:0] WRITE,
  output [2:0] READ,
  output [3:0] FLAGS,
  output [4:0] ALU
);

  wire button_1_out, clock_1_out, ctrl_bus_1_nie, ctrl_bus_1_nwr2, ctrl_condition_checker_1_s,
       ctrl_decoder_1_amux, ctrl_decoder_1_ied, ctrl_decoder_1_imux, ctrl_decoder_1_itog, ctrl_decoder_1_mrd,
       ctrl_decoder_1_mwr, ctrl_decoder_1_nbwr, ctrl_decoder_1_ndae, ctrl_decoder_1_nir, ctrl_decoder_1_rmux,
       ctrl_decoder_1_umi, ctrl_ram_1_nae, ctrl_ram_1_nbuf, ctrl_ram_1_nce, ctrl_ram_1_nde, ctrl_ram_1_noe,
       ctrl_ram_1_nwe, ctrl_reg_decoder_1_pc, fsm_main_1_nirqr, int_manager_1_irq, io_ctrl_1_nioe,
       io_ctrl_1_niwe, io_ctrl_1_nmce, io_ctrl_1_nmoe, io_ctrl_1_nmwe, not_1_out;
  wire [1:0] ctrl_decoder_1_bsel, int_manager_1_oint;
  wire [2:0] ctrl_decoder_1_alu, ctrl_decoder_1_rsel;
  wire [3:0] cpu_1_address, cpu_1_address_2, cpu_1_address_3, cpu_1_address_4, cpu_1_data, cpu_1_data_2,
       cpu_1_data_3, cpu_1_data_4, cpu_1_instr_2, cpu_1_pc_2, cpu_1_pc_2_2, cpu_1_pc_2_3, cpu_1_pc_2_4,
       ctrl_decoder_1_dmux;
  wire [7:0] cpu_1_dout, ram_1_dout, undriven;
  wire [15:0] cpu_1_fpsp, cpu_1_fpsp_2, cpu_1_yfda, cpu_1_yfda_2, cpu_1_yfda_3, cpu_1_yfda_4;
  wire [23:0] cpu_1_opcode;
  wire [27:0] cpu_1_instr;
  wire [31:0] cpu_1_ixiy;

  Clock clock_1 (.out(clock_1_out));
  Counter #(.width(32), .max('hffffffff)) counter_1 (
    .count(nRESET), .clk(clock_1_out), .clr(not_1_out));  // open: load, D, Q, carry
  ctrl_ram ctrl_ram_1 (
    .nAE(ctrl_ram_1_nae), .nCE(ctrl_ram_1_nce), .nBUF(ctrl_ram_1_nbuf), .nWE(ctrl_ram_1_nwe),
    .nOE(ctrl_ram_1_noe), .nDE(ctrl_ram_1_nde), .CLK(clock_1_out), .WR(ctrl_decoder_1_mwr),
    .RD(ctrl_decoder_1_mrd), .nRESET(nRESET));
  TTY #(.rows(16), .cols(40)) tty_1 (.data(cpu_1_dout[6:0]), .clk(io_ctrl_1_niwe), .clr(button_1_out));  // open: we
  Button button_1 (.out(button_1_out));
  not not_1 (not_1_out, nRESET);
  io_ctrl io_ctrl_1 (
    .nCE(ctrl_ram_1_nce), .nOE(ctrl_ram_1_noe), .nWE(ctrl_ram_1_nwe),
    .A({cpu_1_address_4, cpu_1_address_3, cpu_1_address_2, cpu_1_address}), .nIOE(io_ctrl_1_nioe),
    .nIWE(io_ctrl_1_niwe), .nMCE(io_ctrl_1_nmce), .nMOE(io_ctrl_1_nmoe), .nMWE(io_ctrl_1_nmwe));  // open: nICE
  ram ram_1 (
    .A({cpu_1_address_4, cpu_1_address_3, cpu_1_address_2, cpu_1_address}), .nCE(io_ctrl_1_nmce),
    .nWE(io_ctrl_1_nmwe), .nOE(io_ctrl_1_nmoe), .DIN(cpu_1_dout), .DOUT(ram_1_dout));
  int_manager int_manager_1 (
    .CLK(clock_1_out), .TOG(ctrl_decoder_1_itog), .ED(ctrl_decoder_1_ied), .nIRQ(nIRQ),
    .nMR(fsm_main_1_nirqr), .IRQ(int_manager_1_irq), .IINT(IRQN), .OINT(int_manager_1_oint));
  ctrl_bus ctrl_bus_1 (
    .nDE(ctrl_ram_1_nde), .nIE(ctrl_bus_1_nie), .nIR(ctrl_decoder_1_nir), .nWR2(ctrl_bus_1_nwr2),
    .nWR(ctrl_decoder_1_nbwr));
  assign ram_1_dout = io_ctrl_1_nioe ? undriven : 8'bz;  // Controlled_Buffer controlled_buffer_1
  fsm_main fsm_main_1 (
    .nRESET(nRESET), .OPCODE(OPCODE), .COND(ctrl_condition_checker_1_s), .CLK(clock_1_out), .CTR(CTR),
    .STATE(S), .IRQ(int_manager_1_irq), .nIRQR(fsm_main_1_nirqr));
  ctrl_decoder ctrl_decoder_1 (
    .S(S), .OP(OPCODE), .C1(CTR), .nBWR(ctrl_decoder_1_nbwr), .MWR(ctrl_decoder_1_mwr),
    .RSEL(ctrl_decoder_1_rsel), .MRD(ctrl_decoder_1_mrd), .BSEL(ctrl_decoder_1_bsel),
    .AMUX(ctrl_decoder_1_amux), .nDAE(ctrl_decoder_1_ndae), .DMUX(ctrl_decoder_1_dmux),
    .ALU(ctrl_decoder_1_alu), .RMUX(ctrl_decoder_1_rmux), .IMUX(ctrl_decoder_1_imux),
    .nIR(ctrl_decoder_1_nir), .ITOG(ctrl_decoder_1_itog), .IED(ctrl_decoder_1_ied),
    .INTN(int_manager_1_oint), .UMI(ctrl_decoder_1_umi));
  cpu cpu_1 (
    .CLK(clock_1_out), .nAE(ctrl_ram_1_nae), .nBUF(ctrl_ram_1_nbuf), .IS(ctrl_decoder_1_bsel),
    .nWR(ctrl_bus_1_nwr2), .RW(WRITE), .RR(READ), .OPCODE({cpu_1_opcode[23:8], OPCODE, cpu_1_opcode[2:0]}),
    .nDE(ctrl_decoder_1_ndae), .DMUX(ctrl_decoder_1_dmux), .ALU(ALU), .FLAGS(FLAGS),
    .INSTR({cpu_1_instr_2, cpu_1_instr}),
    .ADDRESS({cpu_1_address_4, cpu_1_address_3, cpu_1_address_2, cpu_1_address}),
    .DATA({cpu_1_data_4, cpu_1_data_3, cpu_1_data_2, cpu_1_data}),
    .YFDA({cpu_1_yfda_3[7:0], cpu_1_yfda_4[7:0], cpu_1_yfda[7:0], cpu_1_yfda_2[7:0]}), .nIE(ctrl_bus_1_nie),
    .IMUX(ctrl_decoder_1_imux), .RMUX(ctrl_decoder_1_rmux), .AMUX(ctrl_decoder_1_amux), .DIN(ram_1_dout),
    .DOUT(cpu_1_dout), .PC(ctrl_reg_decoder_1_pc), .FPSP({cpu_1_fpsp_2, cpu_1_fpsp}),
    .PC_2({cpu_1_pc_2_4, cpu_1_pc_2_3, cpu_1_pc_2_2, cpu_1_pc_2}),
    .XECB({cpu_1_yfda_3[15:8], cpu_1_yfda_4[15:8], cpu_1_yfda[15:8], cpu_1_yfda_2[15:8]}), .IXIY(cpu_1_ixiy),
    .UMI(ctrl_decoder_1_umi));  // open: A, B, R
  ctrl_reg_decoder ctrl_reg_decoder_1 (
    .I(ctrl_decoder_1_rsel), .OP({cpu_1_opcode[23:8], OPCODE, cpu_1_opcode[2:0]}), .OW(WRITE), .OR(READ),
    .PC(ctrl_reg_decoder_1_pc));
  ctrl_alu_decoder ctrl_alu_decoder_1 (
    .OPCODE({cpu_1_opcode[23:8], OPCODE, cpu_1_opcode[2:0]}), .I(ctrl_decoder_1_alu), .O(ALU));
  ctrl_condition_checker ctrl_condition_checker_1 (
    .C(FLAGS[0]), .Z(FLAGS[1]), .N(FLAGS[2]), .V(FLAGS[3]), .U(OPCODE[0]), .N_2(cpu_1_opcode[2]),
    .CD(cpu_1_opcode[1:0]), .S(ctrl_condition_checker_1_s));
  Hex_Digit_Display hex_digit_display_1 (.value(cpu_1_instr_2));  // open: dp
  Hex_Digit_Display hex_digit_display_2 (.value(cpu_1_instr[23:20]));  // open: dp
  Hex_Digit_Display hex_digit_display_3 (.value(cpu_1_instr[27:24]));  // open: dp
  Hex_Digit_Display hex_digit_display_4 (.value(cpu_1_instr[19:16]));  // open: dp
  Hex_Digit_Display hex_digit_display_5 (.value(cpu_1_instr[15:12]));  // open: dp
  Hex_Digit_Display hex_digit_display_6 (.value(cpu_1_address_4));  // open: dp
  Hex_Digit_Display hex_digit_display_7 (.value(cpu_1_data_4));  // open: dp
  Hex_Digit_Display hex_digit_display_8 (.value(cpu_1_yfda_2[15:12]));  // open: dp
  Hex_Digit_Display hex_digit_display_9 (.value(cpu_1_yfda_2[11:8]));  // open: dp
  Hex_Digit_Display hex_digit_display_10 (.value(cpu_1_yfda[15:12]));  // open: dp
  Hex_Digit_Display hex_digit_display_11 (.value(cpu_1_yfda[11:8]));  // open: dp
  Hex_Digit_Display hex_digit_display_12 (.value(cpu_1_yfda_4[11:8]));  // open: dp
  Hex_Digit_Display hex_digit_display_13 (.value(cpu_1_yfda_4[15:12]));  // open: dp
  Hex_Digit_Display hex_digit_display_14 (.value(cpu_1_yfda_3[15:12]));  // open: dp
  Hex_Digit_Display hex_digit_display_15 (.value(cpu_1_yfda_3[11:8]));  // open: dp
  Hex_Digit_Display hex_digit_display_16 (.value(cpu_1_instr[7:4]));  // open: dp
  Hex_Digit_Display hex_digit_display_17 (.value(cpu_1_instr[11:8]));  // open: dp
  Hex_Digit_Display hex_digit_display_18 (.value(cpu_1_address_3));  // open: dp
  Hex_Digit_Display hex_digit_display_19 (.value(cpu_1_address_2));  // open: dp
  Hex_Digit_Display hex_digit_display_20 (.value(cpu_1_data_3));  // open: dp
  Hex_Digit_Display hex_digit_display_21 (.value(cpu_1_data_2));  // open: dp
  Hex_Digit_Display hex_digit_display_22 (.value(cpu_1_yfda_2[7:4]));  // open: dp
  Hex_Digit_Display hex_digit_display_23 (.value(cpu_1_yfda_2[3:0]));  // open: dp
  Hex_Digit_Display hex_digit_display_24 (.value(cpu_1_yfda[3:0]));  // open: dp
  Hex_Digit_Display hex_digit_display_25 (.value(cpu_1_yfda[7:4]));  // open: dp
  Hex_Digit_Display hex_digit_display_26 (.value(cpu_1_yfda_4[3:0]));  // open: dp
  Hex_Digit_Display hex_digit_display_27 (.value(cpu_1_yfda_4[7:4]));  // open: dp
  Hex_Digit_Display hex_digit_display_28 (.value(cpu_1_yfda_3[7:4]));  // open: dp
  Hex_Digit_Display hex_digit_display_29 (.value(cpu_1_yfda_3[3:0]));  // open: dp
  Hex_Digit_Display hex_digit_display_30 (.value(cpu_1_instr[3:0]));  // open: dp
  Hex_Digit_Display hex_digit_display_31 (.value(cpu_1_address));  // open: dp
  Hex_Digit_Display hex_digit_display_32 (.value(cpu_1_data));  // open: dp
  Hex_Digit_Display hex_digit_display_33 (.value(cpu_1_pc_2_4));  // open: dp
  Hex_Digit_Display hex_digit_display_34 (.value(cpu_1_fpsp_2[15:12]));  // open: dp
  Hex_Digit_Display hex_digit_display_35 (.value(cpu_1_fpsp[15:12]));  // open: dp
  Hex_Digit_Display hex_digit_display_36 (.value(cpu_1_ixiy[31:28]));  // open: dp
  Hex_Digit_Display hex_digit_display_37 (.value(cpu_1_ixiy[15:12]));  // open: dp
  Hex_Digit_Display hex_digit_display_38 (.value(cpu_1_pc_2_3));  // open: dp
  Hex_Digit_Display hex_digit_display_39 (.value(cpu_1_pc_2_2));  // open: dp
  Hex_Digit_Display hex_digit_display_40 (.value(cpu_1_fpsp_2[11:8]));  // open: dp
  Hex_Digit_Display hex_digit_display_41 (.value(cpu_1_fpsp_2[7:4]));  // open: dp
  Hex_Digit_Display hex_digit_display_42 (.value(cpu_1_fpsp[11:8]));  // open: dp
  Hex_Digit_Display hex_digit_display_43 (.value(cpu_1_fpsp[7:4]));  // open: dp
  Hex_Digit_Display hex_digit_display_44 (.value(cpu_1_ixiy[23:20]));  // open: dp
  Hex_Digit_Display hex_digit_display_45 (.value(cpu_1_ixiy[27:24]));  // open: dp
  Hex_Digit_Display hex_digit_display_46 (.value(cpu_1_ixiy[11:8]));  // open: dp
  Hex_Digit_Display hex_digit_display_47 (.value(cpu_1_ixiy[7:4]));  // open: dp
  Hex_Digit_Display hex_digit_display_48 (.value(cpu_1_pc_2));  // open: dp
  Hex_Digit_Display hex_digit_display_49 (.value(cpu_1_fpsp_2[3:0]));  // open: dp
  Hex_Digit_Display hex_digit_display_50 (.value(cpu_1_fpsp[3:0]));  // open: dp
  Hex_Digit_Display hex_digit_display_51 (.value(cpu_1_ixiy[19:16]));  // open: dp
  Hex_Digit_Display hex_digit_display_52 (.value(cpu_1_ixiy[3:0]));  // open: dp

  // Notes on the sheet:
  //   REG
  //   VNZC
  //   INSTRUCTION
  //   ADDRESS
  //   DATA
  //   B
  //   C
  //   E
  //   X
  //   A
  //   D
  //   F
  //   Y
  //   PC
  //   FP
  //   SP
  //   IY
  //   IX
endmodule

module cpu (
  input  CLK,
  input  nAE,
  input  nBUF,
  input  [1:0] IS,
  input  nIE,
  input  nWR,
  input  PC,
  input  UMI,
  input  [2:0] RW,
  input  [2:0] RR,
  input  nDE,
  input  [3:0] DMUX,
  input  AMUX,
  input  RMUX,
  input  IMUX,
  input  [4:0] ALU,
  input  [7:0] DIN,
  output [3:0] FLAGS,
  output [23:0] OPCODE,
  output [7:0] DOUT,
  output [15:0] R,
  output [15:0] A,
  output [15:0] B,
  output [15:0] ADDRESS,
  output [31:0] INSTR,
  output [31:0] YFDA,
  output [31:0] FPSP,
  output [15:0] DATA,
  output [15:0] PC_2,
  output [31:0] XECB,
  output [31:0] IXIY
);

  wire alu_1__16, not_1_out;
  wire [7:0] multiplexer_2_out, multiplexer_2_out_2;
  wire [15:0] multiplexer_1_out;

  _16_bit_register u_16_bit_register_1 (
    .D1(multiplexer_1_out[15:8]), .CLK(CLK), .nCE1(nAE), .nCE2(nAE), .Q1(ADDRESS[15:8]), .Q2(ADDRESS[7:0]),
    .D2(multiplexer_1_out[7:0]));
  not not_1 (not_1_out, nBUF);
  assign DIN = not_1_out ? multiplexer_2_out : 8'bz;  // Controlled_Buffer controlled_buffer_1
  instr_reg instr_reg_1 (
    .D1(DIN), .CLK(CLK), .nIE(nIE), .IS(IS), .Q1(INSTR[7:0]), .Q2(INSTR[15:8]), .Q3(INSTR[23:16]),
    .Q4(INSTR[31:24]));
  registers registers_1 (
    .LQ(A[7:0]), .nWE(nWR), .LRR(RR), .WR(RW), .LD(DIN), .HQ(A[15:8]), .CLK(CLK), .UWE(alu_1__16),
    .HD(multiplexer_2_out_2), .PC(PC), .YFDA(YFDA), .XECB(XECB), .FPSP(FPSP), .IYIX(IXIY), .PC_2(PC_2),
    .UMI(UMI));
  Multiplexer #(.width(16), .enable("false")) multiplexer_1 (.in0(A), .in1(R), .out(multiplexer_1_out), .sel(AMUX));
  Multiplexer #(.width(16), .enable("false")) multiplexer_2 (
    .in0(A), .in1(R), .out({multiplexer_2_out_2, multiplexer_2_out}), .sel(RMUX));
  _16_bit_register u_16_bit_register_2 (
    .D1(A[15:8]), .CLK(CLK), .nCE1(nDE), .nCE2(nDE), .Q1(DATA[15:8]), .Q2(DATA[7:0]), .D2(A[7:0]));
  alu_mux alu_mux_1 (
    .DL(DATA[7:0]), .DH(DATA[15:8]), .I2(INSTR[15:8]), .I3(INSTR[23:16]), .I3_2(INSTR[31:24]), .O(B),
    .DMUX(DMUX), .INT(IMUX));
  alu alu_1 (
    .C(FLAGS[0]), .Z(FLAGS[1]), .N(FLAGS[2]), .V(FLAGS[3]), .X(ALU[0]), .O0(ALU[1]), .O1(ALU[2]), .M(ALU[3]),
    .T(ALU[4]), .A(A), .B(B), .O(R), .CLK(CLK), ._16(alu_1__16));

  assign DOUT = DIN;
  assign OPCODE = INSTR[23:0];

  // Notes on the sheet:
  //   ADDRESS
  //   BUF
  //   RMUX
  //   INSTRUCTION
  //   DATA BUFFER
endmodule

module registers (
  input  nWE,
  input  [2:0] LRR,
  input  [2:0] WR,
  input  [7:0] LD,
  input  UWE,
  input  [7:0] HD,
  input  CLK,
  input  PC,
  input  UMI,
  output [7:0] LQ,
  output [31:0] XECB,
  output [7:0] HQ,
  output [31:0] YFDA,
  output [31:0] FPSP,
  output [31:0] IYIX,
  output [15:0] PC_2
);

  wire n7486_2_input_xor_x4_1__3__1y, n7486_2_input_xor_x4_1__6__2y, n74138_3_8_decoder_inverting_1_ny0,
       n74138_3_8_decoder_inverting_1_ny1, n74138_3_8_decoder_inverting_1_ny2,
       n74138_3_8_decoder_inverting_1_ny3, n74138_3_8_decoder_inverting_1_ny4,
       n74138_3_8_decoder_inverting_1_ny5, n74138_3_8_decoder_inverting_1_ny6,
       n74138_3_8_decoder_inverting_1_ny7, n74138_3_8_decoder_inverting_2_ny0,
       n74138_3_8_decoder_inverting_2_ny1, n74138_3_8_decoder_inverting_2_ny2,
       n74138_3_8_decoder_inverting_2_ny3, n74157_2_1_multiplexer_x4_1__4__y1,
       n74157_2_1_multiplexer_x4_1__7__y2, n74157_2_1_multiplexer_x4_1__9__y3,
       n74157_2_1_multiplexer_x4_1__12__y4, reg_pc_mux_1_h, reg_pc_mux_1_l;
  wire [7:0] multiplexer_1_out, multiplexer_2_out, multiplexer_3_out, multiplexer_4_out, multiplexer_5_out,
       multiplexer_6_out, multiplexer_8_out;

  _74138___3_8_decoder__inverting u_74138_3_8_decoder_inverting_1 (
    .A0(WR[0]), .A1(WR[1]), .A2(WR[2]), .nE1(nWE), .nE2(PC), .E3(1'b1),
    .nY7(n74138_3_8_decoder_inverting_1_ny7), .nY0(n74138_3_8_decoder_inverting_1_ny0),
    .nY1(n74138_3_8_decoder_inverting_1_ny1), .nY2(n74138_3_8_decoder_inverting_1_ny2),
    .nY3(n74138_3_8_decoder_inverting_1_ny3), .nY4(n74138_3_8_decoder_inverting_1_ny4),
    .nY5(n74138_3_8_decoder_inverting_1_ny5), .nY6(n74138_3_8_decoder_inverting_1_ny6));  // open: GND, VCC
  Multiplexer #(.width(8), .disabled(0), .enable("false")) multiplexer_1 (
    .in0(HD), .in1(LD), .out(multiplexer_1_out), .sel(UMI));
  _74138___3_8_decoder__inverting u_74138_3_8_decoder_inverting_2 (
    .A0(WR[0]), .A1(WR[1]), .A2(nWE), .nE1(n7486_2_input_xor_x4_1__6__2y), .nE2(PC), .E3(1'b1),
    .nY0(n74138_3_8_decoder_inverting_2_ny0), .nY1(n74138_3_8_decoder_inverting_2_ny1),
    .nY2(n74138_3_8_decoder_inverting_2_ny2), .nY3(n74138_3_8_decoder_inverting_2_ny3));  // open: nY7, GND, VCC, nY4, nY5, nY6
  Multiplexer #(.width(8), .enable("false")) multiplexer_2 (
    .in0(LD), .in1(multiplexer_1_out), .out(multiplexer_2_out), .sel(UWE));
  _7486___2_input_XOR_x4 u_7486_2_input_xor_x4_1 (
    ._1__1A(WR[2]), ._2__1B(UWE), ._3__1Y(n7486_2_input_xor_x4_1__3__1y), ._4__2A(1'b1),
    ._5__2B(n7486_2_input_xor_x4_1__3__1y), ._6__2Y(n7486_2_input_xor_x4_1__6__2y),
    ._12__4A(n7486_2_input_xor_x4_1__3__1y));  // open: _7__GND, _14__Vcc, _13__4B, _11__4Y, _10__3B, _9__3A, _8__3Y
  _8bit_register u_8bit_register_1 (.D(LD), .CLK(CLK), .nCE(n74138_3_8_decoder_inverting_1_ny0), .Q(YFDA[7:0]));
  _8bit_register u_8bit_register_2 (.D(LD), .CLK(CLK), .nCE(n74138_3_8_decoder_inverting_1_ny1), .Q(YFDA[15:8]));
  _8bit_register u_8bit_register_3 (.D(LD), .CLK(CLK), .nCE(n74138_3_8_decoder_inverting_1_ny2), .Q(YFDA[23:16]));
  _8bit_register u_8bit_register_4 (.D(LD), .CLK(CLK), .nCE(n74138_3_8_decoder_inverting_1_ny3), .Q(YFDA[31:24]));
  _74157___2_1_multiplexer__x4 u_74157_2_1_multiplexer_x4_1 (
    ._1__S(UWE), ._2__A1(1'b1), ._3__B1(n74138_3_8_decoder_inverting_1_ny4),
    ._4__Y1(n74157_2_1_multiplexer_x4_1__4__y1), ._5__A2(1'b1), ._6__B2(n74138_3_8_decoder_inverting_1_ny5),
    ._7__Y2(n74157_2_1_multiplexer_x4_1__7__y2), ._15__nE(1'b0), ._14__A4(1'b1),
    ._13__B4(n74138_3_8_decoder_inverting_1_ny7), ._12__Y4(n74157_2_1_multiplexer_x4_1__12__y4),
    ._11__A3(1'b1), ._10__B3(n74138_3_8_decoder_inverting_1_ny6), ._9__Y3(n74157_2_1_multiplexer_x4_1__9__y3));  // open: _8__GND, _16__Vcc
  reg_pc_mux reg_pc_mux_1 (.PC(PC), .UWE(UWE), .HR(WR[2]), .WE(nWE), .H(reg_pc_mux_1_h), .L(reg_pc_mux_1_l));
  Multiplexer #(.select(2), .width(8), .enable("false")) multiplexer_3 (
    .in0(YFDA[7:0]), .in1(YFDA[15:8]), .in2(YFDA[23:16]), .in3(YFDA[31:24]), .out(multiplexer_3_out),
    .sel(LRR[1:0]));
  _16_bit_register u_16_bit_register_1 (
    .D1(multiplexer_2_out), .CLK(CLK), .nCE1(reg_pc_mux_1_h), .nCE2(reg_pc_mux_1_l), .Q1(PC_2[15:8]),
    .Q2(PC_2[7:0]), .D2(LD));
  _8bit_register u_8bit_register_5 (
    .D(multiplexer_2_out), .CLK(CLK), .nCE(n74138_3_8_decoder_inverting_2_ny0), .Q(XECB[7:0]));
  _8bit_register u_8bit_register_6 (
    .D(multiplexer_2_out), .CLK(CLK), .nCE(n74138_3_8_decoder_inverting_2_ny1), .Q(XECB[15:8]));
  _8bit_register u_8bit_register_7 (
    .D(multiplexer_2_out), .CLK(CLK), .nCE(n74138_3_8_decoder_inverting_2_ny2), .Q(XECB[23:16]));
  _8bit_register u_8bit_register_8 (
    .D(multiplexer_2_out), .CLK(CLK), .nCE(n74138_3_8_decoder_inverting_2_ny3), .Q(XECB[31:24]));
  _16_bit_register u_16_bit_register_2 (
    .D1(multiplexer_1_out), .CLK(CLK), .nCE1(n74157_2_1_multiplexer_x4_1__4__y1),
    .nCE2(n74157_2_1_multiplexer_x4_1__4__y1), .Q1(FPSP[15:8]), .Q2(FPSP[7:0]), .D2(LD));
  _16_bit_register u_16_bit_register_3 (
    .D1(multiplexer_1_out), .CLK(CLK), .nCE1(n74157_2_1_multiplexer_x4_1__7__y2),
    .nCE2(n74157_2_1_multiplexer_x4_1__7__y2), .Q1(FPSP[31:24]), .Q2(FPSP[23:16]), .D2(LD));
  _16_bit_register u_16_bit_register_4 (
    .D1(multiplexer_1_out), .CLK(CLK), .nCE1(n74157_2_1_multiplexer_x4_1__9__y3),
    .nCE2(n74157_2_1_multiplexer_x4_1__9__y3), .Q1(IYIX[15:8]), .Q2(IYIX[7:0]), .D2(LD));
  _16_bit_register u_16_bit_register_5 (
    .D1(multiplexer_1_out), .CLK(CLK), .nCE1(n74157_2_1_multiplexer_x4_1__12__y4),
    .nCE2(n74157_2_1_multiplexer_x4_1__12__y4), .Q1(IYIX[31:24]), .Q2(IYIX[23:16]), .D2(LD));
  Multiplexer #(.select(3), .width(8), .enable("false")) multiplexer_4 (
    .in0(XECB[7:0]), .in1(XECB[15:8]), .in2(XECB[23:16]), .in3(XECB[31:24]), .in4(FPSP[7:0]),
    .in5(FPSP[23:16]), .in6(IYIX[7:0]), .in7(IYIX[23:16]), .out(multiplexer_4_out), .sel({UWE, LRR[1:0]}));
  Multiplexer #(.width(8), .enable("false")) multiplexer_5 (
    .in0(multiplexer_3_out), .in1(multiplexer_4_out), .out(multiplexer_5_out), .sel(LRR[2]));
  Multiplexer #(.width(8), .enable("false")) multiplexer_6 (
    .in0(PC_2[7:0]), .in1(PC_2[15:8]), .out(multiplexer_6_out), .sel(LRR[2]));
  Multiplexer #(.width(8), .enable("false")) multiplexer_7 (
    .in0(multiplexer_5_out), .in1(multiplexer_6_out), .out(LQ), .sel(PC));
  Multiplexer #(.select(3), .width(8), .enable("false")) multiplexer_8 (
    .in0(XECB[7:0]), .in1(XECB[15:8]), .in2(XECB[23:16]), .in3(XECB[31:24]), .in4(FPSP[15:8]),
    .in5(FPSP[31:24]), .in6(IYIX[15:8]), .in7(IYIX[31:24]), .out(multiplexer_8_out), .sel(LRR));
  Multiplexer #(.width(8), .enable("false")) multiplexer_9 (
    .in0(multiplexer_8_out), .in1(PC_2[15:8]), .out(HQ), .sel(PC));

  // Notes on the sheet:
  //   A
  //   D
  //   F
  //   Y
  //   PC
  //   B
  //   C
  //   E
  //   X
  //   SP
  //   FP
  //   IX
  //   IY
endmodule

module alu (
  input  [15:0] A,
  input  [15:0] B,
  input  T,
  input  M,
  input  O1,
  input  O0,
  input  X,
  input  CLK,
  output [15:0] O,
  output _16,
  output C,
  output Z,
  output N,
  output V
);

  wire alu_arithmetic_1_cout, alu_carry_1_co, alu_carry_2_co, alu_decoder_1_a, alu_decoder_1_ae,
       alu_decoder_1_c, alu_decoder_1_f, alu_decoder_1_m2, alu_decoder_1_n, alu_decoder_1_ze,
       alu_shifter_1_c, and_1_out, not_1_out, undriven_2;
  wire [3:0] alu_decoder_1_s0, multiplexer_1_out, multiplexer_2_out;
  wire [7:0] multiplexer_3_out, multiplexer_4_out, undriven;
  wire [15:0] alu_arithmetic_1_f, alu_shifter_1_b;

  and and_1 (and_1_out, alu_decoder_1_f, alu_decoder_1_ae);
  alu_decoder alu_decoder_1 (
    .T(T), .A(alu_decoder_1_a), .M(M), .O1(O1), .O0(O0), .M2(alu_decoder_1_m2), .X(X),
    .S3(alu_decoder_1_s0[3]), .S2(alu_decoder_1_s0[2]), .S1(alu_decoder_1_s0[1]), .S0(alu_decoder_1_s0[0]),
    .E(_16), .C(alu_decoder_1_c), .N(alu_decoder_1_n), .F(alu_decoder_1_f), .ZE(alu_decoder_1_ze),
    .AE(alu_decoder_1_ae));
  Multiplexer #(.width(4), .enable("false")) multiplexer_1 (
    .in0(multiplexer_2_out), .in1(A[3:0]), .out(multiplexer_1_out), .sel(and_1_out));
  alu_carry alu_carry_1 (.Cin(multiplexer_1_out[0]), .C(1'b0), .N(alu_decoder_1_n), .Co(alu_carry_1_co));
  alu_arithmetic alu_arithmetic_1 (
    .Cin(alu_carry_2_co), .A(A), .B(B), .M(alu_decoder_1_m2), .S(alu_decoder_1_s0),
    .Cout(alu_arithmetic_1_cout), ._16bit(_16), .V(multiplexer_2_out[3]), .F(alu_arithmetic_1_f));
  alu_shifter alu_shifter_1 (.A(A), .D(alu_decoder_1_m2), ._16bit(_16), .B(alu_shifter_1_b), .C(alu_shifter_1_c));
  alu_flags alu_flags_1 (
    .CLK(CLK), .ZE(alu_decoder_1_ze), .AE(alu_decoder_1_ae), .Cout(C), .Zout(Z), .Nout(N), .Vout(V),
    .V(multiplexer_1_out[3]), .N(multiplexer_1_out[2]), .Z(multiplexer_1_out[1]), .Cin(alu_carry_1_co));
  alu_carry alu_carry_2 (.Cin(C), .C(alu_decoder_1_c), .N(alu_decoder_1_n), .Co(alu_carry_2_co));
  Multiplexer #(.enable("false")) multiplexer_2 (
    .in0(alu_shifter_1_c), .in1(alu_arithmetic_1_cout), .out(multiplexer_2_out[0]), .sel(alu_decoder_1_a));
  alu_zero_flag alu_zero_flag_1 (.A({O[15:8], multiplexer_3_out}), ._16(_16), .Z(multiplexer_2_out[1]));
  alu_sign_flag alu_sign_flag_1 (.A({O[15:8], multiplexer_3_out}), ._16(_16), .N(multiplexer_2_out[2]));
  Multiplexer #(.width(16), .enable("false")) multiplexer_3 (
    .in0(alu_shifter_1_b), .in1(alu_arithmetic_1_f), .out({O[15:8], multiplexer_3_out}), .sel(alu_decoder_1_a));
  not not_1 (not_1_out, undriven_2);
  Multiplexer #(.width(8), .enable("false")) multiplexer_4 (
    .in0(undriven), .in1({8{1'b0}}), .out(multiplexer_4_out), .sel(not_1_out));
  Multiplexer #(.width(8), .enable("false")) multiplexer_5 (
    .in0(multiplexer_3_out), .in1({4'b0000, V, N, Z, C}), .out(O[7:0]), .sel(alu_decoder_1_f));
endmodule

module ram (
  input  [15:0] A,
  input  nCE,
  input  nWE,
  input  nOE,
  input  [7:0] DIN,
  output [7:0] DOUT
);

  wire not_1_out, not_2_out, not_3_out;
  wire [7:0] controlled_buffer_1_out;

  not not_1 (not_1_out, nWE);
  assign controlled_buffer_1_out = not_1_out ? DIN : 8'bz;  // Controlled_Buffer controlled_buffer_1
  not not_2 (not_2_out, nOE);
  not not_3 (not_3_out, nCE);
  RAM #(.addrWidth(16), .bus("separate")) ram_1 (
    .addr(A), .din(controlled_buffer_1_out), .data(DOUT), .str(1'b1), .sel(not_3_out), .clk(nWE),
    .ld(not_2_out));  // open: clr
endmodule

module _16_bit_register (
  input  [7:0] D1,
  input  [7:0] D2,
  input  CLK,
  input  nCE1,
  input  nCE2,
  output [7:0] Q1,
  output [7:0] Q2
);

  _8bit_register u_8bit_register_1 (.D(D1), .CLK(CLK), .nCE(nCE1), .Q(Q1));
  _8bit_register u_8bit_register_2 (.D(D2), .CLK(CLK), .nCE(nCE2), .Q(Q2));
endmodule

module instr_reg (
  input  [7:0] D1,
  input  CLK,
  input  nIE,
  input  [1:0] IS,
  output [7:0] Q1,
  output [7:0] Q2,
  output [7:0] Q3,
  output [7:0] Q4
);

  wire not_1_out;
  wire [3:0] n74139_2_4_decoder_inverting_x2_1__1y0;

  not not_1 (not_1_out, CLK);
  _74139___2_4_decoder__inverting__x2 u_74139_2_4_decoder_inverting_x2_1 (
    ._1E(nIE), ._1A0(IS[0]), ._1A1(IS[1]), ._1Y0(n74139_2_4_decoder_inverting_x2_1__1y0[0]),
    ._1Y1(n74139_2_4_decoder_inverting_x2_1__1y0[1]), ._1Y2(n74139_2_4_decoder_inverting_x2_1__1y0[2]),
    ._1Y3(n74139_2_4_decoder_inverting_x2_1__1y0[3]));  // open: GND, VCC, _2E, _2A0, _2A1, _2Y0, _2Y1, _2Y2, _2Y3
  _8bit_register u_8bit_register_1 (.D(D1), .CLK(not_1_out), .nCE(n74139_2_4_decoder_inverting_x2_1__1y0[0]), .Q(Q1));
  _8bit_register u_8bit_register_2 (.D(D1), .CLK(not_1_out), .nCE(n74139_2_4_decoder_inverting_x2_1__1y0[1]), .Q(Q2));
  _8bit_register u_8bit_register_3 (.D(D1), .CLK(not_1_out), .nCE(n74139_2_4_decoder_inverting_x2_1__1y0[2]), .Q(Q3));
  _8bit_register u_8bit_register_4 (.D(D1), .CLK(not_1_out), .nCE(n74139_2_4_decoder_inverting_x2_1__1y0[3]), .Q(Q4));
endmodule

module _8bit_register (
  input  [7:0] D,
  input  CLK,
  input  nCE,
  output [7:0] Q
);

  wire not_1_out;

  not not_1 (not_1_out, nCE);
  Register register_1 (.D(D), .en(not_1_out), .Q(Q), .clk(CLK));  // open: clr
endmodule

module _7402___2_input_NOR_x4 (
  input  _14__Vcc,
  input  _2__1A,
  input  _3__1B,
  input  _12__4B,
  input  _11__4A,
  input  _5__2A,
  input  _6__2B,
  input  _9__3B,
  input  _7__GND,
  input  _8__3A,
  output _1__1Y,
  output _13__4Y,
  output _4__2Y,
  output _10__3Y
);

  nor nor_1 (_1__1Y, _2__1A, _3__1B);
  nor nor_2 (_4__2Y, _5__2A, _6__2B);
  nor nor_3 (_13__4Y, _11__4A, _12__4B);
  nor nor_4 (_10__3Y, _8__3A, _9__3B);

  // Notes on the sheet:
  //   7402: quad NOR
endmodule

module _7408___2_input_AND_x4 (
  input  _1__1A,
  input  _14__Vcc,
  input  _2__1B,
  input  _13__4B,
  input  _12__4A,
  input  _4__2A,
  input  _5__2B,
  input  _10__3B,
  input  _9__3A,
  input  _7__GND,
  output _3__1Y,
  output _11__4Y,
  output _6__2Y,
  output _8__3Y
);

  and and_1 (_3__1Y, _2__1B, _1__1A);
  and and_2 (_6__2Y, _5__2B, _4__2A);
  and and_3 (_11__4Y, _13__4B, _12__4A);
  and and_4 (_8__3Y, _10__3B, _9__3A);

  // Notes on the sheet:
  //   7408: quad AND
endmodule

module _7432___2_input_OR_x4 (
  input  _1__1A,
  input  _14__Vcc,
  input  _2__1B,
  input  _13__4B,
  input  _12__4A,
  input  _4__2A,
  input  _5__2B,
  input  _10__3B,
  input  _9__3A,
  input  _7__GND,
  output _3__1Y,
  output _11__4Y,
  output _6__2Y,
  output _8__3Y
);

  or or_1 (_3__1Y, _2__1B, _1__1A);
  or or_2 (_6__2Y, _5__2B, _4__2A);
  or or_3 (_11__4Y, _13__4B, _12__4A);
  or or_4 (_8__3Y, _10__3B, _9__3A);

  // Notes on the sheet:
  //   7432: quad OR
endmodule

module _7486___2_input_XOR_x4 (
  input  _1__1A,
  input  _14__Vcc,
  input  _2__1B,
  input  _13__4B,
  input  _12__4A,
  input  _4__2A,
  input  _5__2B,
  input  _10__3B,
  input  _9__3A,
  input  _7__GND,
  output _3__1Y,
  output _11__4Y,
  output _6__2Y,
  output _8__3Y
);

  xor xor_1 (_3__1Y, _2__1B, _1__1A);
  xor xor_2 (_6__2Y, _5__2B, _4__2A);
  xor xor_3 (_11__4Y, _13__4B, _12__4A);
  xor xor_4 (_8__3Y, _10__3B, _9__3A);

  // Notes on the sheet:
  //   7486 2 input  XOR
endmodule

module _74181___4_bit_ALU (
  input  nB0,
  input  VCC,
  input  nA0,
  input  nA1,
  input  S3,
  input  nB1,
  input  S2,
  input  nA2,
  input  S1,
  input  nB2,
  input  S0,
  input  nA3,
  input  Cin,
  input  nB3,
  input  M,
  input  GND,
  output nG,
  output nF0,
  output Cout,
  output nF1,
  output nP,
  output nF2,
  output A_B,
  output nF3
);

  wire and_1_out, and_2_out, and_3_out, and_4_out, and_5_out, and_6_out, and_7_out, and_8_out, and_9_out,
       and_10_out, and_11_out, and_12_out, and_13_out, and_14_out, and_15_out, and_16_out, and_17_out,
       and_18_out, and_19_out, and_20_out, and_21_out, and_22_out, and_23_out, and_24_out, and_25_out,
       and_26_out, and_27_out, and_28_out, and_29_out, and_30_out, and_31_out, and_32_out, and_33_out,
       and_34_out, buffer_1_out, buffer_2_out, buffer_3_out, buffer_4_out, buffer_5_out, buffer_6_out,
       buffer_7_out, buffer_8_out, buffer_9_out, buffer_10_out, buffer_11_out, buffer_12_out, buffer_13_out,
       buffer_14_out, nand_1_out, nand_2_out, nand_3_out, nor_1_out, nor_2_out, nor_3_out, nor_4_out,
       nor_5_out, nor_6_out, nor_7_out, nor_8_out, nor_9_out, nor_10_out, nor_11_out, nor_12_out, not_1_out,
       not_2_out, not_3_out, not_4_out, not_5_out, or_1_out, xor_1_out, xor_2_out, xor_3_out, xor_4_out,
       xor_5_out, xor_6_out, xor_7_out, xor_8_out;

  buf buffer_1 (buffer_1_out, S3);
  buf buffer_2 (buffer_2_out, S2);
  buf buffer_3 (buffer_3_out, S1);
  buf buffer_4 (buffer_4_out, S0);
  buf buffer_5 (buffer_5_out, nB3);
  not not_1 (not_1_out, buffer_5_out);
  buf buffer_6 (buffer_6_out, nA3);
  not not_2 (not_2_out, buffer_7_out);
  buf buffer_7 (buffer_7_out, nB2);
  buf buffer_8 (buffer_8_out, nA2);
  buf buffer_9 (buffer_9_out, nB1);
  not not_3 (not_3_out, buffer_9_out);
  buf buffer_10 (buffer_10_out, nA1);
  buf buffer_11 (buffer_11_out, nB0);
  not not_4 (not_4_out, buffer_11_out);
  buf buffer_12 (buffer_12_out, nA0);
  buf buffer_13 (buffer_13_out, M);
  buf buffer_14 (buffer_14_out, Cin);
  not not_5 (not_5_out, buffer_13_out);
  and and_1 (and_1_out, buffer_5_out, buffer_1_out, buffer_6_out);
  and and_2 (and_2_out, buffer_6_out, buffer_2_out, not_1_out);
  and and_3 (and_3_out, not_1_out, buffer_3_out);
  and and_4 (and_4_out, buffer_4_out, buffer_5_out);
  and and_5 (and_5_out, buffer_6_out, buffer_6_out);
  and and_6 (and_6_out, buffer_7_out, buffer_1_out, buffer_8_out);
  and and_7 (and_7_out, buffer_8_out, buffer_2_out, not_2_out);
  and and_8 (and_8_out, not_2_out, buffer_3_out);
  and and_9 (and_9_out, buffer_4_out, buffer_7_out);
  and and_10 (and_10_out, buffer_8_out, buffer_8_out);
  and and_11 (and_11_out, buffer_9_out, buffer_1_out, buffer_10_out);
  and and_12 (and_12_out, buffer_10_out, buffer_2_out, not_3_out);
  and and_13 (and_13_out, not_3_out, buffer_3_out);
  and and_14 (and_14_out, buffer_4_out, buffer_9_out);
  and and_15 (and_15_out, buffer_10_out, buffer_10_out);
  and and_16 (and_16_out, buffer_11_out, buffer_1_out, buffer_12_out);
  and and_17 (and_17_out, buffer_12_out, buffer_2_out, not_4_out);
  and and_18 (and_18_out, not_4_out, buffer_3_out);
  and and_19 (and_19_out, buffer_4_out, buffer_11_out);
  and and_20 (and_20_out, buffer_12_out, buffer_12_out);
  nor nor_1 (nor_1_out, and_1_out, and_2_out);
  nor nor_2 (nor_2_out, and_3_out, and_4_out, and_5_out);
  nor nor_3 (nor_3_out, and_6_out, and_7_out);
  nor nor_4 (nor_4_out, and_8_out, and_9_out, and_10_out);
  nor nor_5 (nor_5_out, and_11_out, and_12_out);
  nor nor_6 (nor_6_out, and_13_out, and_14_out, and_15_out);
  nor nor_7 (nor_7_out, and_16_out, and_17_out);
  nor nor_8 (nor_8_out, and_18_out, and_19_out, and_20_out);
  xor xor_1 (xor_1_out, nor_1_out, nor_2_out);
  xor xor_2 (xor_2_out, nor_3_out, nor_4_out);
  xor xor_3 (xor_3_out, nor_5_out, nor_6_out);
  xor xor_4 (xor_4_out, nor_7_out, nor_8_out);
  and and_21 (and_21_out, nor_2_out, nor_2_out);
  and and_22 (and_22_out, nor_1_out, nor_4_out);
  and and_23 (and_23_out, nor_1_out, nor_3_out, nor_6_out);
  and and_24 (and_24_out, nor_1_out, nor_3_out, nor_5_out, nor_8_out);
  nand nand_1 (nand_1_out, nor_1_out, nor_3_out, nor_5_out, nor_7_out, buffer_14_out);
  nand nand_2 (nand_2_out, nor_1_out, nor_3_out, nor_5_out, nor_7_out);
  and and_25 (and_25_out, buffer_14_out, nor_7_out, nor_5_out, nor_3_out, not_5_out);
  and and_26 (and_26_out, nor_5_out, nor_3_out, nor_8_out, not_5_out);
  and and_27 (and_27_out, nor_3_out, nor_6_out, not_5_out);
  and and_28 (and_28_out, nor_4_out, not_5_out);
  and and_29 (and_29_out, buffer_14_out, nor_7_out, nor_5_out, not_5_out);
  and and_30 (and_30_out, nor_5_out, nor_8_out, not_5_out);
  and and_31 (and_31_out, nor_6_out, not_5_out);
  and and_32 (and_32_out, buffer_14_out, nor_7_out, not_5_out);
  and and_33 (and_33_out, nor_8_out, not_5_out);
  nand nand_3 (nand_3_out, buffer_14_out, not_5_out);
  nor nor_9 (nor_9_out, and_29_out, and_30_out, and_31_out);
  nor nor_10 (nor_10_out, and_32_out, and_33_out);
  xor xor_5 (xor_5_out, xor_4_out, nand_3_out);
  nor nor_11 (nor_11_out, and_21_out, and_22_out, and_23_out, and_24_out);
  or or_1 (or_1_out, ~nor_11_out, ~nand_1_out);  // OR_Gate
  xor xor_6 (xor_6_out, xor_1_out, nor_12_out);
  nor nor_12 (nor_12_out, and_25_out, and_26_out, and_27_out, and_28_out);
  xor xor_7 (xor_7_out, xor_2_out, nor_9_out);
  xor xor_8 (xor_8_out, xor_3_out, nor_10_out);
  and and_34 (and_34_out, xor_6_out, xor_7_out, xor_8_out, xor_5_out);
  buf buffer_15 (nG, nor_11_out);
  buf buffer_16 (Cout, or_1_out);
  buf buffer_17 (nP, nand_2_out);
  buf buffer_18 (nF3, xor_6_out);
  buf buffer_19 (nF2, xor_7_out);
  buf buffer_20 (A_B, and_34_out);
  buf buffer_21 (nF1, xor_8_out);
  buf buffer_22 (nF0, xor_5_out);
endmodule

module _74182___carry_lookahead (
  input  nG1,
  input  VCC,
  input  nP1,
  input  nP2,
  input  nG0,
  input  nG2,
  input  nP0,
  input  Cn,
  input  nG3,
  input  nP3,
  output Cn_x,
  output Cn_y,
  output nP,
  output nG,
  output GND,
  output Cn_z
);

  wire nand_1_out, nand_2_out, nand_3_out, nand_4_out, nand_5_out, nand_6_out, nand_7_out, nand_8_out,
       nand_9_out, nand_10_out, nand_11_out, nand_12_out, nand_13_out, nand_14_out, nand_15_out, nand_16_out,
       nand_17_out, nand_18_out, not_1_out, not_2_out, not_3_out, not_4_out, not_5_out, not_6_out, not_7_out,
       not_8_out, not_9_out, not_10_out, not_11_out, not_12_out, not_13_out, not_14_out, not_15_out,
       not_16_out, not_17_out, not_18_out;

  not not_1 (not_1_out, nP3);
  not not_2 (not_2_out, nG3);
  not not_3 (not_3_out, nP2);
  not not_4 (not_4_out, nG2);
  not not_5 (not_5_out, nP1);
  not not_6 (not_6_out, nG1);
  not not_7 (not_7_out, nP0);
  not not_8 (not_8_out, nG0);
  not not_9 (not_9_out, Cn);
  not not_10 (not_10_out, not_1_out);
  not not_11 (not_11_out, not_2_out);
  not not_12 (not_12_out, not_3_out);
  not not_13 (not_13_out, not_4_out);
  not not_14 (not_14_out, not_5_out);
  not not_15 (not_15_out, not_6_out);
  not not_16 (not_16_out, not_7_out);
  not not_17 (not_17_out, not_8_out);
  not not_18 (not_18_out, nand_1_out);
  nand nand_1 (nand_1_out, not_1_out, not_3_out, not_5_out, not_7_out);
  nand nand_2 (nand_2_out, not_17_out, not_15_out, not_13_out, not_11_out);
  nand nand_3 (nand_3_out, not_14_out, not_15_out, not_13_out, not_11_out);
  nand nand_4 (nand_4_out, not_12_out, not_13_out, not_11_out);
  nand nand_5 (nand_5_out, not_10_out, not_11_out);
  nand nand_6 (nand_6_out, not_13_out, not_15_out, not_17_out, not_9_out);
  nand nand_7 (nand_7_out, not_13_out, not_15_out, not_16_out, not_17_out);
  nand nand_8 (nand_8_out, not_14_out, not_13_out, not_15_out);
  nand nand_9 (nand_9_out, not_12_out, not_13_out);
  nand nand_10 (nand_10_out, not_15_out, not_17_out, not_9_out);
  nand nand_11 (nand_11_out, not_16_out, not_15_out, not_17_out);
  nand nand_12 (nand_12_out, not_14_out, not_15_out);
  nand nand_13 (nand_13_out, not_17_out, not_9_out);
  nand nand_14 (nand_14_out, not_16_out, not_17_out);
  not not_19 (nG, nand_15_out);
  nand nand_15 (nand_15_out, nand_2_out, nand_3_out, nand_4_out, nand_5_out);
  not not_20 (Cn_z, nand_16_out);
  nand nand_16 (nand_16_out, nand_6_out, nand_7_out, nand_8_out, nand_9_out);
  not not_21 (Cn_y, nand_17_out);
  nand nand_17 (nand_17_out, nand_10_out, nand_11_out, nand_12_out);
  nand nand_18 (nand_18_out, nand_13_out, nand_14_out);
  not not_22 (Cn_x, nand_18_out);
  not not_23 (nP, not_18_out);
endmodule

module _74138___3_8_decoder__inverting (
  input  A0,
  input  VCC,
  input  A1,
  input  A2,
  input  nE1,
  input  nE2,
  input  E3,
  output nY0,
  output nY1,
  output nY2,
  output nY3,
  output nY4,
  output nY7,
  output nY5,
  output GND,
  output nY6
);

  wire and_1_out, and_2_out, and_3_out, and_4_out, and_5_out, and_6_out, and_7_out, and_8_out, and_9_out,
       decoder_1_out0, decoder_1_out1, decoder_1_out2, decoder_1_out3, decoder_1_out4, decoder_1_out5,
       decoder_1_out6, decoder_1_out7, not_1_out, not_2_out;

  not not_1 (not_1_out, nE1);
  not not_2 (not_2_out, nE2);
  not not_3 (nY7, and_1_out);
  and and_1 (and_1_out, and_2_out, decoder_1_out7);
  and and_2 (and_2_out, not_1_out, not_2_out, E3);
  Decoder #(.select(3), .enable("false")) decoder_1 (
    .out0(decoder_1_out0), .out1(decoder_1_out1), .out2(decoder_1_out2), .out3(decoder_1_out3),
    .out4(decoder_1_out4), .out5(decoder_1_out5), .out6(decoder_1_out6), .out7(decoder_1_out7),
    .sel({A2, A1, A0}));
  and and_3 (and_3_out, and_2_out, decoder_1_out0);
  not not_4 (nY0, and_3_out);
  not not_5 (nY1, and_4_out);
  and and_4 (and_4_out, and_2_out, decoder_1_out1);
  not not_6 (nY2, and_5_out);
  and and_5 (and_5_out, and_2_out, decoder_1_out2);
  not not_7 (nY3, and_6_out);
  and and_6 (and_6_out, and_2_out, decoder_1_out3);
  and and_7 (and_7_out, and_2_out, decoder_1_out4);
  not not_8 (nY4, and_7_out);
  not not_9 (nY5, and_8_out);
  and and_8 (and_8_out, and_2_out, decoder_1_out5);
  and and_9 (and_9_out, and_2_out, decoder_1_out6);
  not not_10 (nY6, and_9_out);

  // Notes on the sheet:
  //   74138: 3-Line to 8-Line Decoder
endmodule

module _74139___2_4_decoder__inverting__x2 (
  input  _1E,
  input  VCC,
  input  _1A0,
  input  _2E,
  input  _1A1,
  input  _2A0,
  input  _2A1,
  output _1Y0,
  output _1Y1,
  output _2Y0,
  output _1Y2,
  output _2Y1,
  output _1Y3,
  output _2Y2,
  output GND,
  output _2Y3
);

  wire nand_1_out, nand_2_out, nand_3_out, nand_4_out, nand_5_out, nand_6_out, nand_7_out, nand_8_out,
       not_1_out, not_2_out, not_3_out, not_4_out, not_5_out, not_6_out, not_7_out, not_8_out, not_9_out,
       not_10_out, not_11_out, not_12_out, not_13_out, not_14_out, not_15_out, not_16_out, not_17_out,
       not_18_out;

  not not_1 (not_1_out, _1A0);
  not not_2 (not_2_out, _1A1);
  not not_3 (not_3_out, _1E);
  not not_4 (not_4_out, _2A0);
  not not_5 (not_5_out, _2A1);
  not not_6 (not_6_out, _2E);
  not not_7 (not_7_out, not_1_out);
  not not_8 (not_8_out, not_2_out);
  not not_9 (not_9_out, not_4_out);
  not not_10 (not_10_out, not_5_out);
  nand nand_1 (nand_1_out, not_1_out, not_2_out, not_3_out);
  nand nand_2 (nand_2_out, not_7_out, not_2_out, not_3_out);
  nand nand_3 (nand_3_out, not_1_out, not_8_out, not_3_out);
  nand nand_4 (nand_4_out, not_7_out, not_8_out, not_3_out);
  nand nand_5 (nand_5_out, not_4_out, not_5_out, not_6_out);
  nand nand_6 (nand_6_out, not_9_out, not_5_out, not_6_out);
  nand nand_7 (nand_7_out, not_4_out, not_10_out, not_6_out);
  nand nand_8 (nand_8_out, not_9_out, not_10_out, not_6_out);
  not not_11 (not_11_out, nand_1_out);
  not not_12 (not_12_out, nand_2_out);
  not not_13 (not_13_out, nand_3_out);
  not not_14 (not_14_out, nand_4_out);
  not not_15 (not_15_out, nand_5_out);
  not not_16 (not_16_out, nand_6_out);
  not not_17 (not_17_out, nand_7_out);
  not not_18 (not_18_out, nand_8_out);
  not not_19 (_1Y0, not_11_out);
  not not_20 (_1Y1, not_12_out);
  not not_21 (_1Y2, not_13_out);
  not not_22 (_1Y3, not_14_out);
  not not_23 (_2Y0, not_15_out);
  not not_24 (_2Y1, not_16_out);
  not not_25 (_2Y2, not_17_out);
  not not_26 (_2Y3, not_18_out);
endmodule

module _74153___4_1_multiplexer__x2 (
  input  _1E,
  input  VCC,
  input  S1,
  input  _2E,
  input  _1I3,
  input  S0,
  input  _1I2,
  input  _2I3,
  input  _1I1,
  input  _2I2,
  input  _1I0,
  input  _2I1,
  input  _2I0,
  input  GND,
  output _1Y,
  output _2Y
);

  wire not_1_out, not_2_out;

  not not_1 (not_1_out, _1E);
  Multiplexer #(.select(2)) multiplexer_1 (
    .in0(_1I0), .in1(_1I1), .in2(_1I2), .in3(_1I3), .out(_1Y), .sel({S1, S0}), .en(not_1_out));
  not not_2 (not_2_out, _2E);
  Multiplexer #(.select(2)) multiplexer_2 (
    .in0(_2I0), .in1(_2I1), .in2(_2I2), .in3(_2I3), .out(_2Y), .sel({S1, S0}), .en(not_2_out));
endmodule

module _74157___2_1_multiplexer__x4 (
  input  _1__S,
  input  _16__Vcc,
  input  _2__A1,
  input  _15__nE,
  input  _3__B1,
  input  _14__A4,
  input  _13__B4,
  input  _5__A2,
  input  _6__B2,
  input  _11__A3,
  input  _10__B3,
  input  _8__GND,
  output _4__Y1,
  output _12__Y4,
  output _7__Y2,
  output _9__Y3
);

  wire and_1_out, and_2_out, and_3_out, and_4_out, and_5_out, and_6_out, and_7_out, and_8_out, buffer_1_out,
       buffer_2_out, buffer_3_out, buffer_4_out, buffer_5_out, buffer_6_out, buffer_7_out, buffer_8_out,
       buffer_9_out, buffer_10_out, nor_1_out, nor_2_out, nor_3_out, nor_4_out, nor_5_out, nor_6_out,
       not_1_out;

  buf buffer_1 (buffer_1_out, _1__S);
  not not_1 (not_1_out, buffer_1_out);
  buf buffer_2 (buffer_2_out, _2__A1);
  buf buffer_3 (buffer_3_out, _3__B1);
  not not_2 (_4__Y1, nor_1_out);
  nor nor_1 (nor_1_out, and_1_out, and_2_out);
  buf buffer_4 (buffer_4_out, _5__A2);
  buf buffer_5 (buffer_5_out, _6__B2);
  nor nor_2 (nor_2_out, and_3_out, and_4_out);
  not not_3 (_7__Y2, nor_2_out);
  nor nor_3 (nor_3_out, not_1_out, buffer_6_out);
  and and_1 (and_1_out, nor_3_out, buffer_3_out);
  and and_2 (and_2_out, nor_4_out, buffer_2_out);
  and and_3 (and_3_out, nor_3_out, buffer_5_out);
  and and_4 (and_4_out, nor_4_out, buffer_4_out);
  nor nor_4 (nor_4_out, buffer_1_out, buffer_6_out);
  buf buffer_6 (buffer_6_out, _15__nE);
  buf buffer_7 (buffer_7_out, _14__A4);
  buf buffer_8 (buffer_8_out, _13__B4);
  and and_5 (and_5_out, nor_3_out, buffer_8_out);
  nor nor_5 (nor_5_out, and_5_out, and_6_out);
  and and_6 (and_6_out, nor_4_out, buffer_7_out);
  buf buffer_9 (buffer_9_out, _11__A3);
  buf buffer_10 (buffer_10_out, _10__B3);
  and and_7 (and_7_out, nor_3_out, buffer_10_out);
  nor nor_6 (nor_6_out, and_7_out, and_8_out);
  and and_8 (and_8_out, nor_4_out, buffer_9_out);
  not not_4 (_12__Y4, nor_5_out);
  not not_5 (_9__Y3, nor_6_out);

  // Notes on the sheet:
  //   74157: Quad 2-Line to 1-Line Multiplexer
endmodule

module _74158___2_1_multiplexer__inverting__x4 (
  input  _1__S,
  input  _16__Vcc,
  input  _2__A1,
  input  _15__nE,
  input  _3__B1,
  input  _14__A4,
  input  _13__B4,
  input  _5__A2,
  input  _6__B2,
  input  _11__A3,
  input  _10__B3,
  input  _8__GND,
  output _4__Y1,
  output _12__Y4,
  output _7__Y2,
  output _9__Y3
);

  wire and_1_out, and_2_out, and_3_out, and_4_out, and_5_out, and_6_out, and_7_out, and_8_out, buffer_1_out,
       buffer_2_out, buffer_3_out, buffer_4_out, buffer_5_out, buffer_6_out, buffer_7_out, buffer_8_out,
       buffer_9_out, buffer_10_out, nor_3_out, nor_4_out, not_1_out;

  not not_1 (not_1_out, buffer_1_out);
  buf buffer_1 (buffer_1_out, _1__S);
  buf buffer_2 (buffer_2_out, _2__A1);
  buf buffer_3 (buffer_3_out, _3__B1);
  nor nor_1 (_4__Y1, and_1_out, and_2_out);
  buf buffer_4 (buffer_4_out, _5__A2);
  buf buffer_5 (buffer_5_out, _6__B2);
  nor nor_2 (_7__Y2, and_3_out, and_4_out);
  nor nor_3 (nor_3_out, not_1_out, buffer_6_out);
  and and_1 (and_1_out, nor_3_out, buffer_3_out);
  and and_2 (and_2_out, nor_4_out, buffer_2_out);
  and and_3 (and_3_out, nor_3_out, buffer_5_out);
  and and_4 (and_4_out, nor_4_out, buffer_4_out);
  nor nor_4 (nor_4_out, buffer_1_out, buffer_6_out);
  buf buffer_6 (buffer_6_out, _15__nE);
  buf buffer_7 (buffer_7_out, _14__A4);
  buf buffer_8 (buffer_8_out, _13__B4);
  and and_5 (and_5_out, nor_3_out, buffer_8_out);
  nor nor_5 (_12__Y4, and_5_out, and_6_out);
  and and_6 (and_6_out, nor_4_out, buffer_7_out);
  buf buffer_9 (buffer_9_out, _11__A3);
  buf buffer_10 (buffer_10_out, _10__B3);
  and and_7 (and_7_out, nor_3_out, buffer_10_out);
  nor nor_6 (_9__Y3, and_7_out, and_8_out);
  and and_8 (and_8_out, nor_4_out, buffer_9_out);

  // Notes on the sheet:
  //   74158: Quad 2-Line to 1-Line Multiplexer
endmodule

module _74163___4_bit_sync_counter (
  input  nMR,
  input  VCC,
  input  CLK,
  input  D0,
  input  D1,
  input  D2,
  input  D3,
  input  CEP,
  input  CET,
  input  nPE,
  output TC,
  output Q0,
  output Q1,
  output Q2,
  output Q3,
  output GND
);

  wire and_1_out, and_2_out, counter_1_carry, not_1_out, not_2_out;
  wire [3:0] multiplexer_1_out;

  not not_1 (not_1_out, nMR);
  Multiplexer #(.width(4), .enable("false")) multiplexer_1 (
    .in0({D3, D2, D1, D0}), .in1(4'b0000), .out(multiplexer_1_out), .sel(not_1_out));
  and and_1 (and_1_out, CEP, and_2_out, CET);
  not not_2 (not_2_out, and_2_out);
  Counter #(.width(4), .max('hf)) counter_1 (
    .load(not_2_out), .D(multiplexer_1_out), .count(and_1_out), .Q({Q3, Q2, Q1, Q0}),
    .carry(counter_1_carry), .clk(CLK));  // open: clr
  and and_2 (and_2_out, ~not_1_out, nPE);  // AND_Gate
  and and_3 (TC, counter_1_carry, CET);

  // Notes on the sheet:
  //   74163: Synchronous 4-bit Binary Counter with Synchronous Clear 
endmodule

module _74273___8_bit_register_with_reset (
  input  nMR,
  input  VCC,
  input  D0,
  input  D7,
  input  D1,
  input  D6,
  input  D2,
  input  D5,
  input  D3,
  input  D4,
  input  CLK,
  output Q0,
  output Q7,
  output Q1,
  output Q6,
  output Q2,
  output Q5,
  output Q3,
  output Q4,
  output GND
);

  wire buffer_1_out, buffer_2_out, buffer_3_out, buffer_4_out, buffer_5_out, buffer_6_out, buffer_7_out,
       buffer_8_out, not_1_out, not_2_out, not_3_out, not_4_out, not_5_out, not_6_out, not_7_out, not_8_out,
       not_9_out, not_10_out, not_11_out, not_12_out, not_13_out, not_14_out, not_15_out, not_16_out,
       not_17_out, not_18_out, not_19_out;

  not not_1 (not_1_out, CLK);
  not not_2 (not_2_out, nMR);
  not not_3 (not_3_out, not_2_out);
  buf buffer_1 (buffer_1_out, D0);
  not not_4 (not_4_out, not_1_out);
  buf buffer_2 (buffer_2_out, D1);
  D_Flip_Flop d_ff_1 (.clk(not_4_out), .D(buffer_1_out), .Q(Q0), .en(1'b1), .reset(not_5_out));  // open: Qn, preset
  not not_5 (not_5_out, not_3_out);
  not not_6 (not_6_out, not_1_out);
  D_Flip_Flop d_ff_2 (.clk(not_6_out), .D(buffer_2_out), .Q(Q1), .en(1'b1), .reset(not_8_out));  // open: Qn, preset
  not not_7 (not_7_out, not_1_out);
  not not_8 (not_8_out, not_3_out);
  buf buffer_3 (buffer_3_out, D2);
  D_Flip_Flop d_ff_3 (.clk(not_7_out), .D(buffer_3_out), .Q(Q2), .en(1'b1), .reset(not_9_out));  // open: Qn, preset
  not not_9 (not_9_out, not_3_out);
  buf buffer_4 (buffer_4_out, D3);
  D_Flip_Flop d_ff_4 (.clk(not_11_out), .D(buffer_4_out), .Q(Q3), .en(1'b1), .reset(not_10_out));  // open: Qn, preset
  not not_10 (not_10_out, not_3_out);
  not not_11 (not_11_out, not_1_out);
  buf buffer_5 (buffer_5_out, D4);
  D_Flip_Flop d_ff_5 (.clk(not_12_out), .D(buffer_5_out), .Q(Q4), .en(1'b1), .reset(not_13_out));  // open: Qn, preset
  not not_12 (not_12_out, not_1_out);
  not not_13 (not_13_out, not_3_out);
  buf buffer_6 (buffer_6_out, D5);
  not not_14 (not_14_out, not_1_out);
  not not_15 (not_15_out, not_3_out);
  buf buffer_7 (buffer_7_out, D6);
  D_Flip_Flop d_ff_6 (.clk(not_14_out), .D(buffer_6_out), .Q(Q5), .en(1'b1), .reset(not_15_out));  // open: Qn, preset
  not not_16 (not_16_out, not_1_out);
  buf buffer_8 (buffer_8_out, D7);
  D_Flip_Flop d_ff_7 (.clk(not_16_out), .D(buffer_7_out), .Q(Q6), .en(1'b1), .reset(not_17_out));  // open: Qn, preset
  not not_17 (not_17_out, not_3_out);
  not not_18 (not_18_out, not_1_out);
  D_Flip_Flop d_ff_8 (.clk(not_18_out), .D(buffer_8_out), .Q(Q7), .en(1'b1), .reset(not_19_out));  // open: Qn, preset
  not not_19 (not_19_out, not_3_out);
endmodule

module _74595___shift_reg (
  input  VCC,
  input  DS,
  input  nOE,
  input  STCP,
  input  SHCP,
  input  nMR,
  output Q1,
  output Q2,
  output Q0,
  output Q3,
  output Q4,
  output Q5,
  output Q6,
  output Q7,
  output GND,
  output Q7S
);

  wire not_1_out, not_2_out;
  wire [7:0] register_1_q, shift_register_1_q0;

  assign {Q7, Q6, Q5, Q4, Q3, Q2, Q1, Q0} = not_1_out ? register_1_q : 8'bz;  // Controlled_Buffer controlled_buffer_1
  not not_1 (not_1_out, nOE);
  Shift_Register shift_register_1 (
    .shift(1'b1), .in(DS), .clk(SHCP), .out(Q7S), .clr(not_2_out), .q0(shift_register_1_q0[0]),
    .q1(shift_register_1_q0[1]), .q2(shift_register_1_q0[2]), .q3(shift_register_1_q0[3]),
    .q4(shift_register_1_q0[4]), .q5(shift_register_1_q0[5]), .q6(shift_register_1_q0[6]),
    .q7(shift_register_1_q0[7]));  // open: load, d0, d1, d2, d3, d4, d5, d6, d7
  not not_2 (not_2_out, nMR);
  Register register_1 (.D(shift_register_1_q0), .en(1'b1), .Q(register_1_q), .clk(STCP));  // open: clr
endmodule

module _61256___32kb_sram (
  input  A14,
  input  Vcc,
  input  A12,
  input  nWE,
  input  A7,
  input  A13,
  input  A6,
  input  A8,
  input  A5,
  input  A9,
  input  A4,
  input  A11,
  input  A3,
  input  nOE,
  input  A2,
  input  A10,
  input  A1,
  input  nCE,
  input  A0,
  input  D7,
  input  D0,
  input  D6,
  input  D1,
  input  D5,
  input  D2,
  input  D4,
  input  GND,
  input  D3
);
endmodule

module alu_decoder (
  input  T,
  input  M,
  input  O1,
  input  O0,
  input  X,
  output A,
  output M2,
  output S3,
  output S2,
  output S1,
  output S0,
  output E,
  output C,
  output N,
  output F,
  output ZE,
  output AE
);

  wire and_1_out, and_2_out, and_3_out, and_4_out, and_5_out, and_6_out, and_7_out, and_8_out, and_9_out,
       and_10_out, and_11_out, and_12_out, and_13_out, and_14_out, and_15_out, and_16_out, and_17_out,
       and_18_out, and_19_out, and_20_out, and_21_out, and_22_out, and_23_out, and_24_out, and_25_out,
       and_26_out, and_27_out, and_28_out, and_29_out, and_30_out, and_31_out, and_32_out, and_33_out,
       and_35_out, and_36_out, and_37_out, and_38_out, and_39_out, not_1_out, not_2_out, not_3_out,
       not_4_out, not_5_out, not_6_out, not_7_out, not_8_out, not_9_out, not_10_out, not_11_out, not_12_out,
       not_13_out, not_14_out, not_15_out, not_16_out, not_17_out, not_18_out, not_19_out, not_20_out,
       not_21_out, not_22_out, not_23_out, not_24_out, not_25_out, not_26_out, not_27_out, not_28_out,
       not_29_out, not_30_out, not_31_out, not_32_out, not_33_out, not_34_out, not_35_out, not_36_out,
       not_37_out, not_38_out, not_39_out, not_40_out, not_41_out, not_42_out, not_43_out, not_44_out,
       not_45_out, not_46_out, not_47_out, not_48_out, not_49_out, not_50_out, not_51_out, not_52_out,
       not_53_out, not_54_out;

  not not_1 (not_1_out, M);
  not not_2 (not_2_out, O1);
  not not_3 (not_3_out, T);
  not not_4 (not_4_out, M);
  not not_5 (not_5_out, O1);
  not not_6 (not_6_out, T);
  not not_7 (not_7_out, M);
  not not_8 (not_8_out, O0);
  not not_9 (not_9_out, T);
  not not_10 (not_10_out, X);
  not not_11 (not_11_out, T);
  not not_12 (not_12_out, M);
  not not_13 (not_13_out, O1);
  not not_14 (not_14_out, T);
  not not_15 (not_15_out, O0);
  not not_16 (not_16_out, O1);
  not not_17 (not_17_out, T);
  not not_18 (not_18_out, O1);
  not not_19 (not_19_out, O1);
  not not_20 (not_20_out, O0);
  not not_21 (not_21_out, M);
  not not_22 (not_22_out, O0);
  not not_23 (not_23_out, T);
  not not_24 (not_24_out, M);
  not not_25 (not_25_out, O1);
  not not_26 (not_26_out, O0);
  not not_27 (not_27_out, O1);
  not not_28 (not_28_out, T);
  not not_29 (not_29_out, M);
  not not_30 (not_30_out, O1);
  not not_31 (not_31_out, M);
  not not_32 (not_32_out, O1);
  not not_33 (not_33_out, T);
  not not_34 (not_34_out, T);
  not not_35 (not_35_out, O1);
  not not_36 (not_36_out, O0);
  not not_37 (not_37_out, T);
  not not_38 (not_38_out, M);
  not not_39 (not_39_out, T);
  not not_40 (not_40_out, O0);
  not not_41 (not_41_out, T);
  not not_42 (not_42_out, M);
  not not_43 (not_43_out, O1);
  not not_44 (not_44_out, O1);
  not not_45 (not_45_out, T);
  not not_46 (not_46_out, O1);
  not not_47 (not_47_out, X);
  not not_48 (not_48_out, O0);
  not not_49 (not_49_out, X);
  not not_50 (not_50_out, T);
  not not_51 (not_51_out, O0);
  not not_52 (not_52_out, X);
  not not_53 (not_53_out, T);
  not not_54 (not_54_out, M);
  or or_1 (A, not_1_out, not_2_out, T);
  and and_1 (and_1_out, not_3_out, not_4_out, not_5_out);
  and and_2 (and_2_out, not_6_out, not_7_out, not_8_out);
  and and_3 (and_3_out, M, O1, O0);
  and and_4 (and_4_out, T, M);
  and and_5 (and_5_out, not_9_out, not_10_out);
  and and_6 (and_6_out, not_11_out, not_12_out, O0);
  and and_7 (and_7_out, not_13_out, O0);
  and and_8 (and_8_out, not_14_out, O1, not_15_out);
  and and_9 (and_9_out, T, not_16_out);
  and and_10 (and_10_out, not_17_out, not_18_out, O0);
  and and_11 (and_11_out, M, not_19_out, O0);
  and and_12 (and_12_out, M, O1, not_20_out, X);
  and and_13 (and_13_out, T, not_21_out, O1);
  and and_14 (and_14_out, T, O1, not_22_out);
  and and_15 (and_15_out, not_23_out, not_24_out, not_25_out);
  and and_16 (and_16_out, O1, not_26_out);
  and and_17 (and_17_out, M, not_27_out, O0);
  and and_18 (and_18_out, not_28_out, M, O1);
  and and_19 (and_19_out, T, not_29_out, O1);
  and and_20 (and_20_out, T, M, not_30_out);
  and and_21 (and_21_out, not_31_out, not_32_out);
  and and_22 (and_22_out, not_33_out, O0);
  and and_23 (and_23_out, not_34_out, M, O1);
  and and_24 (and_24_out, T, not_35_out, not_36_out);
  and and_25 (and_25_out, not_37_out, not_38_out, O1, O0);
  and and_26 (and_26_out, not_39_out, X);
  and and_27 (and_27_out, M, O0);
  and and_28 (and_28_out, M, O1);
  and and_29 (and_29_out, T, not_40_out);
  and and_30 (and_30_out, not_41_out, not_42_out, O0);
  and and_31 (and_31_out, not_43_out, O0);
  and and_32 (and_32_out, T, not_44_out);
  and and_33 (and_33_out, T, M);
  and and_34 (F, not_45_out, M, not_46_out, not_47_out);
  and and_35 (and_35_out, M, not_48_out, not_49_out);
  and and_36 (and_36_out, M, O1);
  and and_37 (and_37_out, not_50_out, M, not_51_out, not_52_out);
  and and_38 (and_38_out, not_53_out, M, O1);
  and and_39 (and_39_out, T, not_54_out);
  or or_2 (M2, and_1_out, and_2_out, and_3_out, and_4_out);
  or or_3 (S3, and_5_out, and_6_out, and_7_out, and_8_out, and_9_out);
  or or_4 (S2, and_10_out, and_11_out, and_12_out, and_13_out, and_14_out);
  or or_5 (S1, and_15_out, and_16_out, and_17_out, and_18_out, and_19_out, and_20_out);
  or or_6 (S0, and_21_out, and_22_out, and_23_out, and_24_out);
  or or_7 (E, X, and_25_out);
  or or_8 (C, and_26_out, and_27_out, and_28_out, and_29_out);
  or or_9 (N, and_30_out, and_31_out, and_32_out, and_33_out);
  or or_10 (ZE, and_35_out, and_36_out, T);
  or or_11 (AE, and_37_out, and_38_out, and_39_out);
endmodule

module alu_mux (
  input  [3:0] DMUX,
  input  INT,
  input  [7:0] DH,
  input  [7:0] DL,
  input  [7:0] I2,
  input  [7:0] I3,
  input  [7:0] I3_2,
  output [15:0] O
);

  wire [1:0] multiplexer_1_out;

  Multiplexer #(.width(2), .enable("false")) multiplexer_1 (
    .in0(DMUX[1:0]), .in1(2'b01), .out(multiplexer_1_out), .sel(INT));
  Multiplexer #(.select(2), .width(8), .disabled(0), .enable("false")) multiplexer_2 (
    .in0(DL), .in1(I3), .in2(DH), .in3({4'b0001, DMUX[1:0], 2'b00}), .out(O[7:0]), .sel(DMUX[3:2]));
  Multiplexer #(.select(2), .width(8), .disabled(0), .enable("false")) multiplexer_3 (
    .in0(DH), .in1({8{O[7]}}), .in2(I2), .in3(I3_2), .out(O[15:8]), .sel(multiplexer_1_out));
endmodule

module alu_arithmetic (
  input  Cin,
  input  [15:0] A,
  input  [15:0] B,
  input  M,
  input  [3:0] S,
  input  _16bit,
  output [15:0] F,
  output Cout,
  output V
);

  wire alu_16_bit_simple_1_co8, alu_16_bit_simple_1_co16, multiplexer_1_out, multiplexer_2_out,
       multiplexer_3_out, xnor_1_out, xor_1_out;

  and and_1 (V, xor_1_out, xnor_1_out);
  xor xor_1 (xor_1_out, multiplexer_3_out, multiplexer_1_out);
  xnor xnor_1 (xnor_1_out, multiplexer_1_out, multiplexer_2_out);
  Multiplexer #(.enable("false")) multiplexer_1 (.in0(B[7]), .in1(B[15]), .out(multiplexer_1_out), .sel(_16bit));
  Multiplexer #(.enable("false")) multiplexer_2 (.in0(A[7]), .in1(A[15]), .out(multiplexer_2_out), .sel(_16bit));
  alu_16_bit_simple alu_16_bit_simple_1 (
    .M(M), .S(S), .Cin(Cin), .A(A), .B(B), .Co16(alu_16_bit_simple_1_co16), .F(F),
    .Co8(alu_16_bit_simple_1_co8));
  Multiplexer #(.enable("false")) multiplexer_3 (.in0(F[7]), .in1(F[15]), .out(multiplexer_3_out), .sel(_16bit));
  Multiplexer #(.enable("false")) multiplexer_4 (
    .in0(alu_16_bit_simple_1_co8), .in1(alu_16_bit_simple_1_co16), .out(Cout), .sel(_16bit));
endmodule

module alu_shifter (
  input  [15:0] A,
  input  D,
  input  _16bit,
  output C,
  output [15:0] B
);

  wire multiplexer_10_out;

  Multiplexer #(.enable("false")) multiplexer_1 (.in0(A[14]), .in1(1'b0), .out(B[15]), .sel(D));
  Multiplexer #(.enable("false")) multiplexer_2 (.in0(A[13]), .in1(A[15]), .out(B[14]), .sel(D));
  Multiplexer #(.enable("false")) multiplexer_3 (.in0(A[12]), .in1(A[14]), .out(B[13]), .sel(D));
  Multiplexer #(.enable("false")) multiplexer_4 (.in0(A[11]), .in1(A[13]), .out(B[12]), .sel(D));
  Multiplexer #(.enable("false")) multiplexer_5 (.in0(A[10]), .in1(A[12]), .out(B[11]), .sel(D));
  Multiplexer #(.enable("false")) multiplexer_6 (.in0(A[9]), .in1(A[11]), .out(B[10]), .sel(D));
  Multiplexer #(.enable("false")) multiplexer_7 (.in0(A[7]), .in1(A[9]), .out(B[8]), .sel(D));
  Multiplexer #(.enable("false")) multiplexer_8 (.in0(A[8]), .in1(A[10]), .out(B[9]), .sel(D));
  Multiplexer #(.enable("false")) multiplexer_9 (.in0(A[6]), .in1(A[8]), .out(B[7]), .sel(D));
  Multiplexer #(.enable("false")) multiplexer_10 (.in0(A[7]), .in1(A[15]), .out(multiplexer_10_out), .sel(_16bit));
  Multiplexer #(.enable("false")) multiplexer_11 (.in0(A[5]), .in1(A[7]), .out(B[6]), .sel(D));
  Multiplexer #(.enable("false")) multiplexer_12 (.in0(A[3]), .in1(A[5]), .out(B[4]), .sel(D));
  Multiplexer #(.enable("false")) multiplexer_13 (.in0(A[4]), .in1(A[6]), .out(B[5]), .sel(D));
  Multiplexer #(.enable("false")) multiplexer_14 (.in0(multiplexer_10_out), .in1(A[0]), .out(C), .sel(D));
  Multiplexer #(.enable("false")) multiplexer_15 (.in0(A[2]), .in1(A[4]), .out(B[3]), .sel(D));
  Multiplexer #(.enable("false")) multiplexer_16 (.in0(A[1]), .in1(A[3]), .out(B[2]), .sel(D));
  Multiplexer #(.enable("false")) multiplexer_17 (.in0(1'b0), .in1(A[1]), .out(B[0]), .sel(D));
  Multiplexer #(.enable("false")) multiplexer_18 (.in0(A[0]), .in1(A[2]), .out(B[1]), .sel(D));
endmodule

module alu_carry (
  input  Cin,
  input  C,
  input  N,
  output Co
);

  wire and_1_out;

  and and_1 (and_1_out, Cin, ~C);  // AND_Gate
  xor xor_1 (Co, and_1_out, N);
endmodule

module alu_zero_flag (
  input  [15:0] A,
  input  _16,
  output Z
);

  wire nor_1_out, nor_2_out, or_1_out;

  and and_1 (Z, nor_1_out, or_1_out);
  or or_1 (or_1_out, ~_16, nor_2_out);  // OR_Gate
  nor nor_1 (nor_1_out, A[0], A[1], A[2], A[3], A[4], A[5], A[6], A[7]);
  nor nor_2 (nor_2_out, A[8], A[9], A[10], A[11], A[12], A[13], A[14], A[15]);
endmodule

module alu_sign_flag (
  input  [15:0] A,
  input  _16,
  output N
);

  Multiplexer #(.enable("false")) multiplexer_1 (.in0(A[7]), .in1(A[15]), .out(N), .sel(_16));
endmodule

module alu_flags (
  input  CLK,
  input  ZE,
  input  AE,
  input  Cin,
  input  Z,
  input  N,
  input  V,
  output Cout,
  output Zout,
  output Nout,
  output Vout
);

  D_Flip_Flop d_ff_1 (.clk(CLK), .D(Cin), .Q(Cout), .en(AE));  // open: Qn, preset, reset
  D_Flip_Flop d_ff_2 (.clk(CLK), .D(Z), .Q(Zout), .en(ZE));  // open: Qn, preset, reset
  D_Flip_Flop d_ff_3 (.clk(CLK), .D(N), .Q(Nout), .en(AE));  // open: Qn, preset, reset
  D_Flip_Flop d_ff_4 (.clk(CLK), .D(V), .Q(Vout), .en(AE));  // open: Qn, preset, reset

  // Notes on the sheet:
  //   CARRY
  //   ZERO
  //   SIGN
  //   OVERFLOW
endmodule

module alu_16_bit_simple (
  input  Cin,
  input  M,
  input  [3:0] S,
  input  [15:0] A,
  input  [15:0] B,
  output [15:0] F,
  output Co16,
  output Co8
);

  wire alu_4_bit_simple_1_cout, alu_4_bit_simple_3_cout;

  alu_4_bit_simple alu_4_bit_simple_1 (
    .A(A[3:0]), .B(B[3:0]), .M(M), .S(S), .Cin(Cin), .Cout(alu_4_bit_simple_1_cout), .F(F[3:0]));
  alu_4_bit_simple alu_4_bit_simple_2 (
    .A(A[7:4]), .B(B[7:4]), .M(M), .S(S), .Cin(alu_4_bit_simple_1_cout), .Cout(Co8), .F(F[7:4]));
  alu_4_bit_simple alu_4_bit_simple_3 (
    .A(A[11:8]), .B(B[11:8]), .M(M), .S(S), .Cin(Co8), .Cout(alu_4_bit_simple_3_cout), .F(F[11:8]));
  alu_4_bit_simple alu_4_bit_simple_4 (
    .A(A[15:12]), .B(B[15:12]), .M(M), .S(S), .Cin(alu_4_bit_simple_3_cout), .Cout(Co16), .F(F[15:12]));
endmodule

module alu_4_bit_simple (
  input  [3:0] A,
  input  [3:0] B,
  input  M,
  input  [3:0] S,
  input  Cin,
  output Cout,
  output [3:0] F
);

  wire n74181_4_bit_alu_1_a_b;

  _74181___4_bit_ALU u_74181_4_bit_alu_1 (
    .nB0(B[0]), .nA0(A[0]), .S3(S[3]), .S2(S[2]), .S1(S[1]), .S0(S[0]), .Cin(Cin), .M(M), .nF0(F[0]),
    .nF1(F[1]), .nF2(F[2]), .nA1(A[1]), .nB1(B[1]), .nA2(A[2]), .nB2(B[2]), .nA3(A[3]), .nB3(B[3]),
    .Cout(Cout), .A_B(n74181_4_bit_alu_1_a_b), .nF3(F[3]));  // open: GND, VCC, nG, nP
endmodule

module ctrl_condition_checker (
  input  C,
  input  Z,
  input  N,
  input  V,
  input  U,
  input  N_2,
  input  [1:0] CD,
  output S
);

  wire multiplexer_1_out, n7486_2_input_xor_x4_1__3__1y, n7486_2_input_xor_x4_1__6__2y,
       n7486_2_input_xor_x4_1__8__3y, n7486_2_input_xor_x4_1__11__4y, xor_1_out, xor_2_out, xor_3_out,
       xor_4_out;

  xor xor_1 (xor_1_out, C, N_2);
  xor xor_2 (xor_2_out, Z, N_2);
  xor xor_3 (xor_3_out, N, N_2);
  xor xor_4 (xor_4_out, V, N_2);
  _7486___2_input_XOR_x4 u_7486_2_input_xor_x4_1 (
    ._1__1A(C), ._2__1B(N_2), ._3__1Y(n7486_2_input_xor_x4_1__3__1y), ._4__2A(Z), ._5__2B(N_2),
    ._6__2Y(n7486_2_input_xor_x4_1__6__2y), ._13__4B(N_2), ._12__4A(N),
    ._11__4Y(n7486_2_input_xor_x4_1__11__4y), ._10__3B(V), ._9__3A(N_2),
    ._8__3Y(n7486_2_input_xor_x4_1__8__3y));  // open: _7__GND, _14__Vcc
  Multiplexer #(.select(2), .enable("false")) multiplexer_1 (
    .in0(xor_1_out), .in1(xor_2_out), .in2(xor_3_out), .in3(xor_4_out), .out(multiplexer_1_out), .sel(CD));
  Multiplexer #(.enable("false")) multiplexer_2 (.in0(multiplexer_1_out), .in1(1'b1), .out(S), .sel(U));
endmodule

module ctrl_bus (
  input  nDE,
  input  nIR,
  input  nWR,
  output nIE,
  output nWR2
);

  wire and_1_out, and_2_out, not_1_out;

  not not_1 (not_1_out, nIR);
  and and_1 (and_1_out, nIR, nWR);
  and and_2 (and_2_out, nDE, nWR);
  or or_1 (nIE, not_1_out, nDE);
  or or_2 (nWR2, and_1_out, and_2_out);
endmodule

module ctrl_ram (
  input  CLK,
  input  WR,
  input  RD,
  input  nRESET,
  output nAE,
  output nCE,
  output nBUF,
  output nWE,
  output nOE,
  output nDE
);

  wire and_1_out, and_2_out, and_3_out, and_4_out, and_5_out, d_ff_1_q, d_ff_2_q, d_ff_3_q, nor_1_out,
       nor_2_out, not_1_out, not_2_out, or_1_out, or_2_out, or_3_out, or_4_out;

  and and_1 (and_1_out, ~d_ff_1_q, WR);  // AND_Gate
  or or_1 (or_1_out, and_1_out, d_ff_1_q);
  or or_2 (or_2_out, d_ff_1_q, and_2_out);
  and and_2 (and_2_out, ~d_ff_1_q, ~WR, RD);  // AND_Gate
  and and_3 (and_3_out, ~d_ff_2_q, or_1_out);  // AND_Gate
  and and_4 (and_4_out, ~d_ff_2_q, or_2_out);  // AND_Gate
  D_Flip_Flop d_ff_1 (.clk(CLK), .D(and_3_out), .Q(d_ff_1_q));  // open: Qn, preset, en, reset
  D_Flip_Flop d_ff_2 (.clk(CLK), .D(and_4_out), .Q(d_ff_2_q));  // open: Qn, preset, en, reset
  D_Flip_Flop d_ff_3 (.clk(not_1_out), .D(or_4_out), .Q(d_ff_3_q));  // open: Qn, preset, en, reset
  not not_1 (not_1_out, CLK);
  not not_2 (not_2_out, CLK);
  D_Flip_Flop d_ff_4 (.clk(not_2_out), .D(nOE));  // open: Q, Qn, preset, en, reset
  or or_3 (or_3_out, d_ff_1_q, d_ff_2_q);
  nor nor_1 (nor_1_out, d_ff_2_q, d_ff_1_q);
  and and_5 (and_5_out, d_ff_2_q, ~d_ff_1_q);  // AND_Gate
  or or_4 (or_4_out, d_ff_2_q, ~d_ff_1_q);  // OR_Gate
  or or_5 (nOE, ~d_ff_2_q, d_ff_1_q);  // OR_Gate
  nor nor_2 (nor_2_out, WR, RD);
  or or_6 (nAE, nor_2_out, or_3_out);
  Multiplexer #(.enable("false")) multiplexer_1 (.in0(1'b1), .in1(nor_1_out), .out(nCE), .sel(nRESET));
  Multiplexer #(.enable("false")) multiplexer_2 (.in0(1'b0), .in1(and_5_out), .out(nBUF), .sel(nRESET));
  Multiplexer #(.enable("false")) multiplexer_3 (.in0(1'b1), .in1(d_ff_3_q), .out(nWE), .sel(nRESET));
  Multiplexer #(.enable("false")) multiplexer_4 (.in0(1'b1), .in1(nOE), .out(nDE), .sel(nRESET));
endmodule

module ctrl_reg_decoder (
  input  [23:0] OP,
  input  [2:0] I,
  output [2:0] OW,
  output [2:0] OR,
  output PC
);

  Multiplexer #(.select(3), .width(3), .enable("false")) multiplexer_1 (
    .in0(OP[2:0]), .in1(3'b000), .in2(3'b100), .in3(3'b011), .in4(3'b000), .in5(3'b000), .in6(OP[2:0]),
    .in7(3'b111), .out(OW), .sel(I));
  Multiplexer #(.select(3), .width(3), .enable("false")) multiplexer_2 (
    .in0(OP[15:13]), .in1(3'b000), .in2(3'b100), .in3(3'b011), .in4(3'b000), .in5(OP[23:21]), .in6(OP[2:0]),
    .in7(3'b111), .out(OR), .sel(I));
  and and_1 (PC, I[1], I[0]);

  // Notes on the sheet:
  //   FAKE
  //   FAKE
endmodule

module ctrl_alu_decoder (
  input  [23:0] OPCODE,
  input  [2:0] I,
  output [4:0] O
);

  wire [4:0] undriven;

  Multiplexer #(.select(3), .width(5), .enable("false")) multiplexer_1 (
    .in0({5{1'b0}}), .in1(5'b00001), .in2(5'b01001), .in3(5'b01011), .in4(5'b00101), .in5(OPCODE[12:8]),
    .in6(OPCODE[7:3]), .in7(undriven), .out(O), .sel(I));
endmodule

module ctrl_decoder (
  input  [1:0] INTN,
  input  [2:0] S,
  input  [4:0] OP,
  input  [2:0] C1,
  output [1:0] BSEL,
  output nIR,
  output IMUX,
  output [3:0] DMUX,
  output nDAE,
  output AMUX,
  output RMUX,
  output ITOG,
  output IED,
  output UMI,
  output MRD,
  output MWR,
  output nBWR,
  output [2:0] RSEL,
  output [2:0] ALU
);

  wire and_1_out, and_2_out, and_3_out, and_4_out, and_5_out, and_8_out, and_9_out, and_10_out, and_11_out,
       and_12_out, and_13_out, and_14_out, and_15_out, and_16_out, and_17_out, and_18_out, nor_1_out,
       or_1_out, or_2_out, or_3_out, or_4_out, or_5_out, or_6_out, or_7_out;
  wire [3:0] ctrl_decoder_dmux_1_dmux0;
  wire [10:0] undriven, undriven_3;
  wire [10:3] undriven_2;

  nor nor_1 (nor_1_out, undriven[10], undriven[0]);
  and and_1 (and_1_out, ~undriven[7], undriven[5], ~undriven[4], ~undriven[3]);  // AND_Gate
  and and_2 (and_2_out, undriven[7], undriven[6], ~undriven[5], undriven[4]);  // AND_Gate
  and and_3 (and_3_out, ~undriven[7], ~undriven[6], ~undriven[5], ~undriven[4], undriven[3]);  // AND_Gate
  and and_4 (and_4_out, ~undriven_2[7], undriven_2[4], undriven_2[3]);  // AND_Gate
  and and_5 (and_5_out, undriven_2[7], ~undriven_2[4]);  // AND_Gate
  ctrl_decoder_dmux ctrl_decoder_dmux_1 (
    .O4(OP[4]), .DMUX3(ctrl_decoder_dmux_1_dmux0[3]), .O3(OP[3]), .O2(OP[2]), .O1(OP[1]), .O0(OP[0]),
    .C2(C1[2]), .DMUX2(ctrl_decoder_dmux_1_dmux0[2]), .C1(C1[1]), .C0(C1[0]),
    .DMUX1(ctrl_decoder_dmux_1_dmux0[1]), .DMUX0(ctrl_decoder_dmux_1_dmux0[0]));
  ctrl_decoder_sub ctrl_decoder_sub_1 (
    .S2(S[2]), .S1(S[1]), .S0(S[0]), .O4(OP[4]), .O3(OP[3]), .MRD(MRD), .O2(OP[2]), .O1(OP[1]), .O0(OP[0]),
    .C2(C1[2]), .C1(C1[1]), .C0(C1[0]), .MWR(MWR), .RE(nBWR), .REG2(RSEL[2]), .REG1(RSEL[1]), .REG0(RSEL[0]),
    .ALU2(ALU[2]), .ALU1(ALU[1]), .ALU0(ALU[0]));
  and and_6 (nIR, S[2], ~S[1], S[0]);  // AND_Gate
  and and_7 (IMUX, S[2], S[1], ~S[0]);  // AND_Gate
  or or_1 (or_1_out, and_1_out, and_2_out, and_3_out);
  and and_8 (and_8_out, undriven_2[10], ~undriven_2[9]);  // AND_Gate
  and and_9 (and_9_out, ~undriven_2[10], undriven_2[6], undriven_2[5]);  // AND_Gate
  or or_2 (or_2_out, and_4_out, and_5_out);
  and and_10 (and_10_out, undriven_3[10], undriven_3[9], ~undriven_3[8]);  // AND_Gate
  and and_11 (and_11_out, ~undriven_3[10], undriven_3[7], undriven_3[6], undriven_3[5], undriven_3[4]);  // AND_Gate
  and and_12 (and_12_out, ~undriven_3[2], undriven_3[1], ~undriven_3[0]);  // AND_Gate
  and and_13 (and_13_out, undriven_3[2], ~undriven_3[1]);  // AND_Gate
  and and_14 (and_14_out, ~undriven_3[10], undriven_3[7], ~undriven_3[6], undriven_3[4], undriven_3[1]);  // AND_Gate
  or or_3 (or_3_out, undriven_3[5], undriven_3[3]);
  and and_15 (and_15_out, nor_1_out, or_1_out);
  and and_16 (and_16_out, and_9_out, or_2_out);
  or or_4 (or_4_out, and_10_out, and_11_out);
  or or_5 (or_5_out, and_12_out, and_13_out);
  nor nor_2 (ITOG, S[2], OP[4], OP[3], OP[2], ~OP[1]);  // NOR_Gate
  Multiplexer #(.width(4), .enable("false")) multiplexer_1 (
    .in0(ctrl_decoder_dmux_1_dmux0), .in1({2'b11, INTN}), .out(DMUX), .sel(IMUX));
  ctrl_decoder_sub2 ctrl_decoder_sub2_1 (
    .S2(S[2]), .S1(S[1]), .S0(S[0]), .O4(OP[4]), .O3(OP[3]), .O2(OP[2]), .O1(OP[1]), .O0(OP[0]), .C2(C1[2]),
    .C1(C1[1]), .C0(C1[0]), .RMUX(RMUX), .AMUX(AMUX), .DAE(nDAE));
  or or_6 (or_6_out, and_8_out, and_16_out);
  and and_17 (and_17_out, or_4_out, or_5_out);
  and and_18 (and_18_out, and_14_out, or_3_out);
  and and_19 (UMI, ~S[2], ~OP[4], OP[3], ~OP[2], OP[1], OP[0], ~C1[1], C1[0]);  // AND_Gate
  // NOT_Gate not_1 has open pins: in=and_15_out, out=open
  // NOT_Gate not_2 has open pins: in=or_6_out, out=open
  not not_3 (IED, OP[0]);
  // NOT_Gate not_4 has open pins: in=or_7_out, out=open
  or or_7 (or_7_out, and_17_out, and_18_out);

  assign BSEL = C1[1:0];
endmodule

module ctrl_decoder_dmux (
  input  O4,
  input  O3,
  input  O2,
  input  O1,
  input  O0,
  input  C2,
  input  C1,
  input  C0,
  output DMUX3,
  output DMUX2,
  output DMUX1,
  output DMUX0
);

  wire and_2_out, and_3_out, and_4_out, and_5_out, and_6_out, and_7_out, and_8_out, and_9_out, and_10_out,
       and_11_out, and_12_out, and_13_out, and_14_out, and_15_out, and_16_out, and_17_out, and_18_out,
       and_19_out, and_20_out, and_21_out, and_22_out, not_1_out, not_2_out, not_3_out, not_4_out, not_5_out,
       not_6_out, not_7_out, not_8_out, not_9_out, not_10_out, not_11_out, not_12_out, not_13_out,
       not_14_out, not_15_out, not_16_out, not_17_out, not_18_out, not_19_out, not_20_out, not_21_out,
       not_22_out, not_23_out, not_24_out, not_25_out, not_26_out, not_27_out, not_28_out, not_29_out,
       not_30_out, not_31_out, not_32_out;

  not not_1 (not_1_out, O4);
  not not_2 (not_2_out, O2);
  not not_3 (not_3_out, O1);
  not not_4 (not_4_out, C0);
  not not_5 (not_5_out, O0);
  not not_6 (not_6_out, C0);
  not not_7 (not_7_out, C0);
  not not_8 (not_8_out, O2);
  not not_9 (not_9_out, O1);
  not not_10 (not_10_out, O3);
  not not_11 (not_11_out, O2);
  not not_12 (not_12_out, O1);
  not not_13 (not_13_out, O0);
  not not_14 (not_14_out, C0);
  not not_15 (not_15_out, O3);
  not not_16 (not_16_out, O2);
  not not_17 (not_17_out, O1);
  not not_18 (not_18_out, O1);
  not not_19 (not_19_out, O3);
  not not_20 (not_20_out, O2);
  not not_21 (not_21_out, O1);
  not not_22 (not_22_out, O4);
  not not_23 (not_23_out, O2);
  not not_24 (not_24_out, O3);
  not not_25 (not_25_out, C2);
  not not_26 (not_26_out, O3);
  not not_27 (not_27_out, C1);
  not not_28 (not_28_out, O3);
  not not_29 (not_29_out, C0);
  not not_30 (not_30_out, O4);
  not not_31 (not_31_out, O4);
  not not_32 (not_32_out, O0);
  and and_1 (DMUX3, not_1_out, not_2_out, not_3_out, not_4_out);
  and and_2 (and_2_out, not_5_out, not_6_out);
  and and_3 (and_3_out, O1, not_7_out);
  and and_4 (and_4_out, O2, O0);
  and and_5 (and_5_out, O2, O1);
  and and_6 (and_6_out, O3, not_8_out, not_9_out, C2, C0);
  and and_7 (and_7_out, O4, not_10_out);
  and and_8 (and_8_out, O4, not_11_out, not_12_out);
  and and_9 (and_9_out, not_13_out, not_14_out);
  and and_10 (and_10_out, not_15_out, O1, C0);
  and and_11 (and_11_out, O2, O1, C0);
  and and_12 (and_12_out, O3, not_16_out, not_17_out, C2, C0);
  and and_13 (and_13_out, O4, O3, not_18_out);
  and and_14 (and_14_out, O4, O3, O2);
  and and_15 (and_15_out, not_19_out, not_20_out, not_21_out);
  and and_16 (and_16_out, not_22_out, not_23_out, C2, C0);
  and and_17 (and_17_out, not_24_out, O0, not_25_out);
  and and_18 (and_18_out, not_26_out, O0, not_27_out);
  and and_19 (and_19_out, not_28_out, O0, not_29_out);
  and and_20 (and_20_out, not_30_out, O1);
  and and_21 (and_21_out, not_31_out, O2, O0);
  and and_22 (and_22_out, O4, O2, not_32_out, C2, C1, C0);
  or or_1 (DMUX2, and_2_out, and_3_out, and_4_out, and_5_out, and_6_out, and_7_out, and_8_out);
  or or_2 (DMUX1, and_9_out, and_10_out, and_11_out, and_12_out, and_13_out, and_14_out);
  or or_3 (DMUX0, and_15_out, and_16_out, and_17_out, and_18_out, and_19_out, and_20_out, and_21_out, and_22_out);
endmodule

module ctrl_decoder_sub (
  input  S2,
  input  S1,
  input  S0,
  input  O4,
  input  O3,
  input  O2,
  input  O1,
  input  O0,
  input  C2,
  input  C1,
  input  C0,
  output MRD,
  output MWR,
  output RE,
  output REG2,
  output REG1,
  output REG0,
  output ALU2,
  output ALU1,
  output ALU0
);

  wire and_1_out, and_2_out, and_3_out, and_4_out, and_5_out, and_6_out, and_7_out, and_8_out, and_9_out,
       and_10_out, and_11_out, and_12_out, and_13_out, and_14_out, and_15_out, and_16_out, and_17_out,
       and_18_out, and_19_out, and_20_out, and_21_out, and_22_out, and_23_out, and_24_out, and_25_out,
       and_26_out, and_27_out, and_28_out, and_29_out, and_30_out, and_31_out, and_32_out, and_33_out,
       and_34_out, and_35_out, and_36_out, and_37_out, and_38_out, and_39_out, and_40_out, and_41_out,
       and_42_out, and_43_out, and_44_out, and_45_out, and_46_out, and_47_out, and_48_out, and_49_out,
       and_50_out, and_51_out, and_52_out, and_53_out, and_54_out, and_55_out, and_56_out, and_57_out,
       and_58_out, and_59_out, and_60_out, and_61_out, and_62_out, and_63_out, and_64_out, and_65_out,
       and_66_out, and_67_out, and_68_out, and_69_out, and_70_out, and_71_out, and_72_out, and_73_out,
       and_74_out, and_75_out, and_76_out, and_77_out, and_78_out, and_79_out, and_80_out, and_81_out,
       and_82_out, and_83_out, and_84_out, and_85_out, and_86_out, and_87_out, and_88_out, and_89_out,
       and_90_out, and_91_out, and_92_out, and_93_out, and_94_out, and_95_out, and_96_out, and_97_out,
       and_98_out, and_99_out, and_100_out, and_101_out, and_102_out, and_103_out, and_104_out, not_1_out,
       not_2_out, not_3_out, not_4_out, not_5_out, not_6_out, not_7_out, not_8_out, not_9_out, not_10_out,
       not_11_out, not_12_out, not_13_out, not_14_out, not_15_out, not_16_out, not_17_out, not_18_out,
       not_19_out, not_20_out, not_21_out, not_22_out, not_23_out, not_24_out, not_25_out, not_26_out,
       not_27_out, not_28_out, not_29_out, not_30_out, not_31_out, not_32_out, not_33_out, not_34_out,
       not_35_out, not_36_out, not_37_out, not_38_out, not_39_out, not_40_out, not_41_out, not_42_out,
       not_43_out, not_44_out, not_45_out, not_46_out, not_47_out, not_48_out, not_49_out, not_50_out,
       not_51_out, not_52_out, not_53_out, not_54_out, not_55_out, not_56_out, not_57_out, not_58_out,
       not_59_out, not_60_out, not_61_out, not_62_out, not_63_out, not_64_out, not_65_out, not_66_out,
       not_67_out, not_68_out, not_69_out, not_70_out, not_71_out, not_72_out, not_73_out, not_74_out,
       not_75_out, not_76_out, not_77_out, not_78_out, not_79_out, not_80_out, not_81_out, not_82_out,
       not_83_out, not_84_out, not_85_out, not_86_out, not_87_out, not_88_out, not_89_out, not_90_out,
       not_91_out, not_92_out, not_93_out, not_94_out, not_95_out, not_96_out, not_97_out, not_98_out,
       not_99_out, not_100_out, not_101_out, not_102_out, not_103_out, not_104_out, not_105_out, not_106_out,
       not_107_out, not_108_out, not_109_out, not_110_out, not_111_out, not_112_out, not_113_out,
       not_114_out, not_115_out, not_116_out, not_117_out, not_118_out, not_119_out, not_120_out,
       not_121_out, not_122_out, not_123_out, not_124_out, not_125_out, not_126_out, not_127_out,
       not_128_out, not_129_out, not_130_out, not_131_out, not_132_out, not_133_out, not_134_out,
       not_135_out, not_136_out, not_137_out, not_138_out, not_139_out, not_140_out, not_141_out,
       not_142_out, not_143_out, not_144_out, not_145_out, not_146_out, not_147_out, not_148_out,
       not_149_out, not_150_out, not_151_out, not_152_out, not_153_out, not_154_out, not_155_out,
       not_156_out, not_157_out, not_158_out, not_159_out, not_160_out, not_161_out, not_162_out,
       not_163_out, not_164_out, not_165_out, not_166_out, not_167_out, not_168_out, not_169_out,
       not_170_out, not_171_out, not_172_out, not_173_out, not_174_out, not_175_out, not_176_out,
       not_177_out, not_178_out, not_179_out, not_180_out, not_181_out, not_182_out, not_183_out,
       not_184_out, not_185_out, not_186_out, not_187_out, not_188_out, not_189_out, not_190_out,
       not_191_out, not_192_out, not_193_out, not_194_out, not_195_out, not_196_out, not_197_out,
       not_198_out, not_199_out, not_200_out, not_201_out, not_202_out, not_203_out, not_204_out,
       not_205_out, not_206_out, not_207_out, not_208_out, not_209_out, not_210_out, not_211_out,
       not_212_out, not_213_out, not_214_out, not_215_out, not_216_out, not_217_out, not_218_out,
       not_219_out, not_220_out, not_221_out, not_222_out, not_223_out, not_224_out, not_225_out,
       not_226_out, not_227_out, not_228_out, not_229_out, not_230_out, not_231_out, not_232_out,
       not_233_out, not_234_out, not_235_out, not_236_out, not_237_out, not_238_out, not_239_out,
       not_240_out, not_241_out, not_242_out, not_243_out, not_244_out, not_245_out, not_246_out,
       not_247_out, not_248_out, not_249_out, not_250_out, not_251_out, not_252_out, not_253_out,
       not_254_out, not_255_out, not_256_out, not_257_out, not_258_out, not_259_out, not_260_out,
       not_261_out, not_262_out, not_263_out, not_264_out, not_265_out, not_266_out, not_267_out,
       not_268_out, not_269_out, not_270_out, not_271_out, not_272_out, not_273_out, not_274_out,
       not_275_out, not_276_out, not_277_out, not_278_out, not_279_out, not_280_out, not_281_out,
       not_282_out, not_283_out, not_284_out, not_285_out, not_286_out, not_287_out;

  not not_1 (not_1_out, S2);
  not not_2 (not_2_out, O4);
  not not_3 (not_3_out, S2);
  not not_4 (not_4_out, O4);
  not not_5 (not_5_out, C0);
  not not_6 (not_6_out, S2);
  not not_7 (not_7_out, O1);
  not not_8 (not_8_out, S2);
  not not_9 (not_9_out, O4);
  not not_10 (not_10_out, O2);
  not not_11 (not_11_out, O1);
  not not_12 (not_12_out, C2);
  not not_13 (not_13_out, S2);
  not not_14 (not_14_out, O4);
  not not_15 (not_15_out, O2);
  not not_16 (not_16_out, O1);
  not not_17 (not_17_out, C1);
  not not_18 (not_18_out, C0);
  not not_19 (not_19_out, S2);
  not not_20 (not_20_out, O4);
  not not_21 (not_21_out, O3);
  not not_22 (not_22_out, O2);
  not not_23 (not_23_out, O0);
  not not_24 (not_24_out, S2);
  not not_25 (not_25_out, O4);
  not not_26 (not_26_out, O3);
  not not_27 (not_27_out, O2);
  not not_28 (not_28_out, C0);
  not not_29 (not_29_out, S2);
  not not_30 (not_30_out, O4);
  not not_31 (not_31_out, O1);
  not not_32 (not_32_out, O0);
  not not_33 (not_33_out, C0);
  not not_34 (not_34_out, S2);
  not not_35 (not_35_out, O3);
  not not_36 (not_36_out, S2);
  not not_37 (not_37_out, O3);
  not not_38 (not_38_out, S2);
  not not_39 (not_39_out, O4);
  not not_40 (not_40_out, O1);
  not not_41 (not_41_out, O0);
  not not_42 (not_42_out, S2);
  not not_43 (not_43_out, O4);
  not not_44 (not_44_out, O1);
  not not_45 (not_45_out, C2);
  not not_46 (not_46_out, C0);
  not not_47 (not_47_out, S2);
  not not_48 (not_48_out, O4);
  not not_49 (not_49_out, O1);
  not not_50 (not_50_out, S2);
  not not_51 (not_51_out, O4);
  not not_52 (not_52_out, O2);
  not not_53 (not_53_out, S2);
  not not_54 (not_54_out, O4);
  not not_55 (not_55_out, O1);
  not not_56 (not_56_out, S2);
  not not_57 (not_57_out, O4);
  not not_58 (not_58_out, O0);
  not not_59 (not_59_out, S2);
  not not_60 (not_60_out, O3);
  not not_61 (not_61_out, S2);
  not not_62 (not_62_out, C1);
  not not_63 (not_63_out, S2);
  not not_64 (not_64_out, C1);
  not not_65 (not_65_out, S2);
  not not_66 (not_66_out, O2);
  not not_67 (not_67_out, C0);
  not not_68 (not_68_out, S2);
  not not_69 (not_69_out, C2);
  not not_70 (not_70_out, C0);
  not not_71 (not_71_out, S0);
  not not_72 (not_72_out, C1);
  not not_73 (not_73_out, S0);
  not not_74 (not_74_out, C2);
  not not_75 (not_75_out, C0);
  not not_76 (not_76_out, S0);
  not not_77 (not_77_out, C1);
  not not_78 (not_78_out, S2);
  not not_79 (not_79_out, O4);
  not not_80 (not_80_out, O3);
  not not_81 (not_81_out, O2);
  not not_82 (not_82_out, S2);
  not not_83 (not_83_out, O4);
  not not_84 (not_84_out, O2);
  not not_85 (not_85_out, O1);
  not not_86 (not_86_out, O0);
  not not_87 (not_87_out, S2);
  not not_88 (not_88_out, O4);
  not not_89 (not_89_out, O2);
  not not_90 (not_90_out, O1);
  not not_91 (not_91_out, C2);
  not not_92 (not_92_out, C0);
  not not_93 (not_93_out, S2);
  not not_94 (not_94_out, O4);
  not not_95 (not_95_out, O2);
  not not_96 (not_96_out, O1);
  not not_97 (not_97_out, S2);
  not not_98 (not_98_out, O4);
  not not_99 (not_99_out, O2);
  not not_100 (not_100_out, S2);
  not not_101 (not_101_out, O3);
  not not_102 (not_102_out, S2);
  not not_103 (not_103_out, O3);
  not not_104 (not_104_out, O1);
  not not_105 (not_105_out, O0);
  not not_106 (not_106_out, C0);
  not not_107 (not_107_out, S2);
  not not_108 (not_108_out, O4);
  not not_109 (not_109_out, O1);
  not not_110 (not_110_out, S2);
  not not_111 (not_111_out, O1);
  not not_112 (not_112_out, C1);
  not not_113 (not_113_out, S2);
  not not_114 (not_114_out, O4);
  not not_115 (not_115_out, O1);
  not not_116 (not_116_out, S2);
  not not_117 (not_117_out, O4);
  not not_118 (not_118_out, O0);
  not not_119 (not_119_out, S2);
  not not_120 (not_120_out, O3);
  not not_121 (not_121_out, O0);
  not not_122 (not_122_out, S2);
  not not_123 (not_123_out, S0);
  not not_124 (not_124_out, C1);
  not not_125 (not_125_out, O4);
  not not_126 (not_126_out, O2);
  not not_127 (not_127_out, O1);
  not not_128 (not_128_out, O4);
  not not_129 (not_129_out, O2);
  not not_130 (not_130_out, O3);
  not not_131 (not_131_out, O2);
  not not_132 (not_132_out, O1);
  not not_133 (not_133_out, O0);
  not not_134 (not_134_out, C0);
  not not_135 (not_135_out, O1);
  not not_136 (not_136_out, S2);
  not not_137 (not_137_out, O3);
  not not_138 (not_138_out, C1);
  not not_139 (not_139_out, S2);
  not not_140 (not_140_out, O3);
  not not_141 (not_141_out, O1);
  not not_142 (not_142_out, O0);
  not not_143 (not_143_out, C0);
  not not_144 (not_144_out, S2);
  not not_145 (not_145_out, O2);
  not not_146 (not_146_out, O1);
  not not_147 (not_147_out, S2);
  not not_148 (not_148_out, O2);
  not not_149 (not_149_out, S2);
  not not_150 (not_150_out, O1);
  not not_151 (not_151_out, C0);
  not not_152 (not_152_out, C1);
  not not_153 (not_153_out, S2);
  not not_154 (not_154_out, O4);
  not not_155 (not_155_out, O3);
  not not_156 (not_156_out, O1);
  not not_157 (not_157_out, S2);
  not not_158 (not_158_out, O4);
  not not_159 (not_159_out, O1);
  not not_160 (not_160_out, S2);
  not not_161 (not_161_out, O4);
  not not_162 (not_162_out, O0);
  not not_163 (not_163_out, S2);
  not not_164 (not_164_out, O3);
  not not_165 (not_165_out, O1);
  not not_166 (not_166_out, C0);
  not not_167 (not_167_out, S2);
  not not_168 (not_168_out, O3);
  not not_169 (not_169_out, C1);
  not not_170 (not_170_out, C0);
  not not_171 (not_171_out, S2);
  not not_172 (not_172_out, O4);
  not not_173 (not_173_out, O0);
  not not_174 (not_174_out, S2);
  not not_175 (not_175_out, O2);
  not not_176 (not_176_out, O1);
  not not_177 (not_177_out, C2);
  not not_178 (not_178_out, C1);
  not not_179 (not_179_out, C0);
  not not_180 (not_180_out, S2);
  not not_181 (not_181_out, O2);
  not not_182 (not_182_out, O1);
  not not_183 (not_183_out, S2);
  not not_184 (not_184_out, O2);
  not not_185 (not_185_out, O1);
  not not_186 (not_186_out, S2);
  not not_187 (not_187_out, O2);
  not not_188 (not_188_out, O1);
  not not_189 (not_189_out, S2);
  not not_190 (not_190_out, O2);
  not not_191 (not_191_out, O0);
  not not_192 (not_192_out, S2);
  not not_193 (not_193_out, O2);
  not not_194 (not_194_out, S2);
  not not_195 (not_195_out, S0);
  not not_196 (not_196_out, S2);
  not not_197 (not_197_out, O4);
  not not_198 (not_198_out, C0);
  not not_199 (not_199_out, S2);
  not not_200 (not_200_out, O4);
  not not_201 (not_201_out, O2);
  not not_202 (not_202_out, C2);
  not not_203 (not_203_out, C1);
  not not_204 (not_204_out, S2);
  not not_205 (not_205_out, O4);
  not not_206 (not_206_out, O2);
  not not_207 (not_207_out, C1);
  not not_208 (not_208_out, C0);
  not not_209 (not_209_out, S2);
  not not_210 (not_210_out, O3);
  not not_211 (not_211_out, O2);
  not not_212 (not_212_out, C1);
  not not_213 (not_213_out, C0);
  not not_214 (not_214_out, S2);
  not not_215 (not_215_out, O1);
  not not_216 (not_216_out, C0);
  not not_217 (not_217_out, S2);
  not not_218 (not_218_out, C2);
  not not_219 (not_219_out, C1);
  not not_220 (not_220_out, C0);
  not not_221 (not_221_out, S2);
  not not_222 (not_222_out, S2);
  not not_223 (not_223_out, O3);
  not not_224 (not_224_out, O1);
  not not_225 (not_225_out, C0);
  not not_226 (not_226_out, S2);
  not not_227 (not_227_out, O4);
  not not_228 (not_228_out, O1);
  not not_229 (not_229_out, C2);
  not not_230 (not_230_out, C1);
  not not_231 (not_231_out, S2);
  not not_232 (not_232_out, O4);
  not not_233 (not_233_out, O1);
  not not_234 (not_234_out, C1);
  not not_235 (not_235_out, C0);
  not not_236 (not_236_out, S2);
  not not_237 (not_237_out, O3);
  not not_238 (not_238_out, C1);
  not not_239 (not_239_out, C0);
  not not_240 (not_240_out, S2);
  not not_241 (not_241_out, C2);
  not not_242 (not_242_out, C1);
  not not_243 (not_243_out, C0);
  not not_244 (not_244_out, S2);
  not not_245 (not_245_out, O4);
  not not_246 (not_246_out, O1);
  and and_1 (and_1_out, not_1_out, not_2_out, O2, O1, O0);
  and and_2 (and_2_out, not_3_out, not_4_out, O3, O1, O0, not_5_out);
  and and_3 (and_3_out, not_6_out, O4, O2, not_7_out);
  and and_4 (and_4_out, S2, not_247_out);
  not not_247 (not_247_out, S1);
  not not_248 (not_248_out, S2);
  not not_249 (not_249_out, O3);
  not not_250 (not_250_out, S2);
  not not_251 (not_251_out, O3);
  not not_252 (not_252_out, S2);
  not not_253 (not_253_out, C2);
  not not_254 (not_254_out, S0);
  not not_255 (not_255_out, C2);
  and and_5 (and_5_out, not_19_out, not_20_out, not_21_out, not_22_out, not_23_out);
  and and_6 (and_6_out, not_24_out, not_25_out, not_26_out, not_27_out, not_28_out);
  and and_7 (and_7_out, not_29_out, not_30_out, not_31_out, not_32_out, not_33_out);
  and and_8 (and_8_out, not_34_out, not_35_out, O1, O0, C0);
  and and_9 (and_9_out, not_36_out, not_37_out, O1, O0, C1);
  and and_10 (and_10_out, not_38_out, not_39_out, O3, not_40_out, not_41_out);
  and and_11 (and_11_out, not_42_out, not_43_out, O3, not_44_out, not_45_out, not_46_out);
  and and_12 (and_12_out, not_47_out, not_48_out, O3, not_49_out, C1);
  and and_13 (and_13_out, not_50_out, not_51_out, O3, not_52_out, O0, C2, C0);
  and and_14 (and_14_out, not_53_out, not_54_out, O3, O2, not_55_out);
  and and_15 (and_15_out, not_56_out, not_57_out, O3, O2, not_58_out);
  and and_16 (and_16_out, not_59_out, O4, not_60_out, O2);
  and and_17 (and_17_out, not_61_out, O4, O2, O1, not_62_out, C0);
  and and_18 (and_18_out, not_63_out, O4, O2, O1, C2, not_64_out);
  and and_19 (and_19_out, not_65_out, O4, O3, not_66_out, O1, not_67_out);
  and and_20 (and_20_out, not_68_out, O4, O3, O1, not_69_out, C1, not_70_out);
  and and_21 (and_21_out, S2, not_256_out, S0);
  not not_256 (not_256_out, S1);
  and and_22 (and_22_out, S2, S1, not_71_out, not_72_out, C0);
  and and_23 (and_23_out, S2, S1, not_73_out, not_74_out, C1, not_75_out);
  and and_24 (and_24_out, S2, S1, not_76_out, C2, not_77_out);
  and and_25 (and_25_out, not_78_out, not_79_out, not_80_out, not_81_out);
  and and_26 (and_26_out, not_82_out, not_83_out, not_84_out, not_85_out, not_86_out);
  and and_27 (and_27_out, not_87_out, not_88_out, not_89_out, not_90_out, not_91_out, not_92_out);
  and and_28 (and_28_out, not_93_out, not_94_out, not_95_out, not_96_out, C1);
  and and_29 (and_29_out, not_97_out, not_98_out, not_99_out, O1, O0, C0);
  and and_30 (and_30_out, not_100_out, not_101_out, O1, O0, C1);
  and and_31 (and_31_out, not_102_out, not_103_out, O2, not_104_out, not_105_out, not_106_out);
  and and_32 (and_32_out, not_107_out, not_108_out, O3, not_109_out, C1, C0);
  and and_33 (and_33_out, not_110_out, O3, O2, not_111_out, not_112_out, C0);
  and and_34 (and_34_out, not_113_out, not_114_out, O3, O2, not_115_out, O0);
  and and_35 (and_35_out, not_116_out, not_117_out, O3, O2, O1, not_118_out);
  and and_36 (and_36_out, not_119_out, O4, not_120_out, O2, O1, not_121_out);
  and and_37 (and_37_out, not_122_out, O4, O2, O1, C2, C0);
  and and_38 (and_38_out, S2, S1, not_123_out, C2, not_124_out);
  and and_39 (and_39_out, not_125_out, not_126_out, not_127_out);
  and and_40 (and_40_out, not_128_out, not_129_out, O0);
  and and_41 (and_41_out, not_130_out, not_131_out, O1, O0);
  and and_42 (and_42_out, O3, not_132_out, O0);
  and and_43 (and_43_out, O3, O2, not_133_out, C0);
  and and_44 (and_44_out, O3, O2, O1, not_134_out);
  and and_45 (and_45_out, O4, O2, O1, C1);
  and and_46 (and_46_out, O4, O3, not_135_out);
  and and_47 (and_47_out, O4, O3, C0);
  and and_48 (and_48_out, not_136_out, not_137_out, O1, O0, not_138_out, C0);
  and and_49 (and_49_out, not_139_out, not_140_out, O2, not_141_out, not_142_out, not_143_out);
  and and_50 (and_50_out, not_144_out, O4, O3, not_145_out, not_146_out);
  and and_51 (and_51_out, not_147_out, O4, O3, not_148_out, C0);
  and and_52 (and_52_out, not_149_out, O4, O3, not_150_out, C0);
  and and_53 (and_53_out, O4, O3, O2, O1, C1, not_151_out);
  and and_54 (and_54_out, O4, O3, O2, O1, C2, not_152_out);
  and and_55 (and_55_out, S2, not_257_out);
  not not_257 (not_257_out, S1);
  and and_56 (and_56_out, S2, C1, not_258_out);
  not not_258 (not_258_out, C0);
  and and_57 (and_57_out, S2, C2);
  and and_58 (and_58_out, S2, S0);
  and and_59 (and_59_out, not_153_out, not_154_out, not_155_out, not_156_out, O0, C0);
  and and_60 (and_60_out, not_157_out, not_158_out, O2, not_159_out);
  and and_61 (and_61_out, not_160_out, not_161_out, O2, not_162_out);
  and and_62 (and_62_out, not_163_out, not_164_out, O2, not_165_out, not_166_out);
  and and_63 (and_63_out, not_167_out, not_168_out, O2, not_169_out, not_170_out);
  and and_64 (and_64_out, not_171_out, not_172_out, O3, not_173_out);
  and and_65 (and_65_out, not_174_out, O3, not_175_out, not_176_out, not_177_out, not_178_out, not_179_out);
  and and_66 (and_66_out, not_180_out, O3, not_181_out, not_182_out, C1, C0);
  and and_67 (and_67_out, not_183_out, O3, not_184_out, not_185_out, C2, C1);
  and and_68 (and_68_out, not_186_out, O4, not_187_out, not_188_out);
  and and_69 (and_69_out, not_189_out, O4, not_190_out, not_191_out);
  and and_70 (and_70_out, not_192_out, O4, O3, not_193_out);
  and and_71 (and_71_out, not_194_out, O4, O3, O1, C2, C1);
  and and_72 (and_72_out, S2, S1, not_195_out, C2, C1);
  not not_259 (not_259_out, S2);
  not not_260 (not_260_out, O4);
  not not_261 (not_261_out, O2);
  not not_262 (not_262_out, O0);
  not not_263 (not_263_out, S2);
  not not_264 (not_264_out, O4);
  not not_265 (not_265_out, O2);
  not not_266 (not_266_out, S1);
  not not_267 (not_267_out, S0);
  not not_268 (not_268_out, S0);
  not not_269 (not_269_out, C2);
  not not_270 (not_270_out, C1);
  not not_271 (not_271_out, C0);
  not not_272 (not_272_out, S0);
  not not_273 (not_273_out, S2);
  not not_274 (not_274_out, O4);
  not not_275 (not_275_out, O1);
  not not_276 (not_276_out, S2);
  not not_277 (not_277_out, O4);
  not not_278 (not_278_out, O0);
  not not_279 (not_279_out, S2);
  not not_280 (not_280_out, O3);
  not not_281 (not_281_out, O2);
  not not_282 (not_282_out, O1);
  not not_283 (not_283_out, S2);
  not not_284 (not_284_out, O2);
  not not_285 (not_285_out, C2);
  not not_286 (not_286_out, C1);
  not not_287 (not_287_out, C0);
  or or_1 (MRD, and_1_out, and_2_out, and_3_out, and_4_out);
  and and_73 (and_73_out, not_8_out, not_9_out, O3, not_10_out, not_11_out, O0, not_12_out, C0);
  and and_74 (and_74_out, not_13_out, not_14_out, O3, not_15_out, not_16_out, O0, C2, not_17_out, not_18_out);
  and and_75 (and_75_out, not_248_out, O4, not_249_out, O1, O0);
  and and_76 (and_76_out, not_250_out, O4, not_251_out, O2, O1);
  and and_77 (and_77_out, not_252_out, O4, O2, O1, not_253_out);
  and and_78 (and_78_out, S2, S1, not_254_out, not_255_out);
  and and_79 (and_79_out, not_196_out, not_197_out, O2, O1, O0, not_198_out);
  and and_80 (and_80_out, not_259_out, not_260_out, O3, not_261_out, not_262_out);
  and and_81 (and_81_out, not_199_out, not_200_out, O3, not_201_out, not_202_out, not_203_out, C0);
  and and_82 (and_82_out, not_204_out, not_205_out, O3, not_206_out, C2, not_207_out, not_208_out);
  and and_83 (and_83_out, not_263_out, not_264_out, O3, not_265_out, O1);
  and and_84 (and_84_out, not_209_out, O4, not_210_out, not_211_out, O1, O0, not_212_out, not_213_out);
  and and_85 (and_85_out, not_214_out, O4, O3, O2, not_215_out, not_216_out);
  and and_86 (and_86_out, not_217_out, O4, O3, O2, not_218_out, not_219_out, not_220_out);
  and and_87 (and_87_out, not_221_out, O4, O3, O2, O1, C1, C0);
  and and_88 (and_88_out, S2, not_266_out, not_267_out);
  and and_89 (and_89_out, S2, not_268_out, not_269_out, not_270_out, not_271_out);
  and and_90 (and_90_out, S2, not_272_out, C1, C0);
  and and_91 (and_91_out, not_273_out, not_274_out, O2, not_275_out);
  and and_92 (and_92_out, not_276_out, not_277_out, O2, not_278_out);
  and and_93 (and_93_out, not_222_out, not_223_out, O2, not_224_out, O0, not_225_out);
  and and_94 (and_94_out, not_226_out, not_227_out, O3, not_228_out, O0, not_229_out, not_230_out, C0);
  and and_95 (and_95_out, not_231_out, not_232_out, O3, not_233_out, O0, C2, not_234_out, not_235_out);
  and and_96 (and_96_out, not_279_out, O4, not_280_out, not_281_out, not_282_out);
  and and_97 (and_97_out, not_236_out, O4, not_237_out, O0, not_238_out, not_239_out);
  and and_98 (and_98_out, not_283_out, O4, O3, not_284_out, O1);
  and and_99 (and_99_out, not_240_out, O4, O3, O1, not_241_out, not_242_out, not_243_out);
  and and_100 (and_100_out, not_244_out, O4, O3, O1, C1, C0);
  and and_101 (and_101_out, S1, not_245_out, O3, not_246_out, O0, C2, C1, C0);
  and and_102 (and_102_out, S2, S1, not_285_out, not_286_out, not_287_out);
  and and_103 (and_103_out, S2, S1, C1, C0);
  and and_104 (and_104_out, S2, S1, S0);
  or or_2 (MWR, and_73_out, and_74_out, and_75_out, and_76_out, and_77_out, and_78_out);
  or or_3 (RE, and_5_out, and_6_out, and_7_out, and_8_out, and_9_out, and_10_out, and_11_out, and_12_out, and_13_out, and_14_out, and_15_out, and_16_out, and_17_out, and_18_out, and_19_out, and_20_out, and_21_out, and_22_out, and_23_out, and_24_out);
  or or_4 (REG2, and_25_out, and_26_out, and_27_out, and_28_out, and_29_out, and_30_out, and_31_out, and_32_out, and_33_out, and_34_out, and_35_out, and_36_out, and_37_out, and_38_out);
  or or_5 (REG1, and_39_out, and_40_out, and_41_out, and_42_out, and_43_out, and_44_out, and_45_out, and_46_out, and_47_out, S2);
  or or_6 (REG0, and_48_out, and_49_out, and_50_out, and_51_out, and_52_out, and_53_out, and_54_out, and_55_out, and_56_out, and_57_out, and_58_out);
  or or_7 (ALU2, and_59_out, and_60_out, and_61_out, and_62_out, and_63_out, and_64_out, and_65_out, and_66_out, and_67_out, and_68_out, and_69_out, and_70_out, and_71_out, and_72_out);
  or or_8 (ALU1, and_79_out, and_80_out, and_81_out, and_82_out, and_83_out, and_84_out, and_85_out, and_86_out, and_87_out, and_88_out, and_89_out, and_90_out);
  or or_9 (ALU0, and_91_out, and_92_out, and_93_out, and_94_out, and_95_out, and_96_out, and_97_out, and_98_out, and_99_out, and_100_out, and_101_out, and_102_out, and_103_out, and_104_out);
endmodule
module ctrl_decoder_sub2 (
  input  S2,
  input  S1,
  input  S0,
  input  O4,
  input  O3,
  input  O2,
  input  O1,
  input  O0,
  input  C2,
  input  C1,
  input  C0,
  output RMUX,
  output AMUX,
  output DAE
);

  wire and_1_out, and_2_out, and_3_out, and_4_out, and_5_out, and_6_out, and_7_out, and_8_out, and_9_out,
       and_10_out, and_11_out, and_12_out, and_13_out, and_14_out, and_15_out, and_16_out, and_17_out,
       and_18_out, and_19_out, and_20_out, and_21_out, and_22_out, and_23_out, and_24_out, not_1_out,
       not_2_out, not_3_out, not_4_out, not_5_out, not_6_out, not_7_out, not_8_out, not_9_out, not_10_out,
       not_11_out, not_12_out, not_13_out, not_14_out, not_15_out, not_16_out, not_17_out, not_18_out,
       not_19_out, not_20_out, not_21_out, not_22_out, not_23_out, not_24_out, not_25_out, not_26_out,
       not_27_out, not_28_out, not_29_out, not_30_out, not_31_out, not_32_out, not_33_out;

  not not_1 (not_1_out, S2);
  not not_2 (not_2_out, O4);
  not not_3 (not_3_out, C0);
  not not_4 (not_4_out, S2);
  not not_5 (not_5_out, O2);
  not not_6 (not_6_out, O0);
  not not_7 (not_7_out, S2);
  not not_8 (not_8_out, O1);
  not not_9 (not_9_out, C1);
  not not_10 (not_10_out, C0);
  not not_11 (not_11_out, S2);
  not not_12 (not_12_out, O4);
  not not_13 (not_13_out, C0);
  not not_14 (not_14_out, S2);
  not not_15 (not_15_out, O2);
  not not_16 (not_16_out, C1);
  not not_17 (not_17_out, S1);
  not not_18 (not_18_out, C2);
  not not_19 (not_19_out, C0);
  not not_20 (not_20_out, S2);
  not not_21 (not_21_out, O4);
  not not_22 (not_22_out, O1);
  not not_23 (not_23_out, S2);
  not not_24 (not_24_out, O3);
  not not_25 (not_25_out, S2);
  not not_26 (not_26_out, O2);
  not not_27 (not_27_out, O1);
  not not_28 (not_28_out, O0);
  not not_29 (not_29_out, O4);
  not not_30 (not_30_out, O3);
  not not_31 (not_31_out, O1);
  not not_32 (not_32_out, O1);
  not not_33 (not_33_out, O1);
  and and_1 (and_1_out, not_1_out, not_2_out, not_3_out);
  and and_2 (and_2_out, not_4_out, not_5_out, not_6_out);
  and and_3 (and_3_out, not_7_out, not_8_out);
  and and_4 (and_4_out, not_9_out, not_10_out);
  and and_5 (and_5_out, not_11_out, not_12_out, O2);
  and and_6 (and_6_out, O3, C2, not_13_out);
  and and_7 (and_7_out, not_14_out, O4, not_15_out, not_16_out);
  and and_8 (and_8_out, O4, O3, C1, C0);
  and and_9 (and_9_out, S2, not_17_out);
  and and_10 (and_10_out, S2, not_18_out, C0);
  and and_11 (and_11_out, S2, C2, not_19_out);
  and and_12 (and_12_out, S2, S0);
  and and_13 (and_13_out, not_20_out, not_21_out, not_22_out);
  and and_14 (and_14_out, not_23_out, not_24_out);
  and and_15 (and_15_out, not_25_out, O4, O1);
  and and_16 (and_16_out, S2, S1);
  and and_17 (and_17_out, not_26_out, not_27_out, not_28_out);
  and and_18 (and_18_out, not_29_out, O1);
  and and_19 (and_19_out, not_30_out, O1);
  and and_20 (and_20_out, O2, O0);
  and and_21 (and_21_out, O2, O1);
  and and_22 (and_22_out, O3, not_31_out, O0, C1);
  and and_23 (and_23_out, O3, not_32_out, O0, C2);
  and and_24 (and_24_out, O4, not_33_out);
  or or_1 (AMUX, and_13_out, and_14_out, and_15_out, and_16_out);
  or or_2 (RMUX, and_1_out, and_2_out, and_3_out, and_4_out, and_5_out, and_6_out, and_7_out, and_8_out, and_9_out, and_10_out, and_11_out, and_12_out);
  or or_3 (DAE, and_17_out, C0, and_18_out, and_19_out, and_20_out, and_21_out, and_22_out, and_23_out, and_24_out, S2);
endmodule

module int_manager (
  input  CLK,
  input  TOG,
  input  ED,
  input  nIRQ,
  input  nMR,
  input  [1:0] IINT,
  output IRQ,
  output [1:0] OINT
);

  wire and_1_out, d_ff_1_q, not_1_out, not_2_out;

  and and_1 (and_1_out, CLK, TOG);
  not not_1 (not_1_out, nIRQ);
  D_Flip_Flop d_ff_1 (.clk(and_1_out), .D(ED), .Q(d_ff_1_q), .en(1'b1));  // open: Qn, preset, reset
  D_Flip_Flop d_ff_2 (.clk(not_1_out), .D(d_ff_1_q), .Q(IRQ), .en(1'b1), .reset(not_2_out));  // open: Qn, preset
  not not_2 (not_2_out, nMR);
  D_Flip_Flop d_ff_3 (.clk(not_1_out), .D(IINT[1]), .Q(OINT[1]), .en(1'b1));  // open: Qn, preset, reset
  D_Flip_Flop d_ff_4 (.clk(not_1_out), .D(IINT[0]), .Q(OINT[0]), .en(1'b1));  // open: Qn, preset, reset
endmodule

module io_ctrl (
  input  nCE,
  input  nOE,
  input  nWE,
  input  [15:0] A,
  output nICE,
  output nIOE,
  output nIWE,
  output nMCE,
  output nMOE,
  output nMWE
);

  wire and_1_out;

  and and_1 (and_1_out, A[10], A[11], A[12], A[13], A[14], A[15]);
  nand nand_1 (nICE, ~nCE, and_1_out);  // NAND_Gate
  nand nand_2 (nIOE, ~nOE, and_1_out);  // NAND_Gate
  nand nand_3 (nIWE, ~nWE, and_1_out);  // NAND_Gate
  or or_1 (nMCE, nCE, and_1_out);
  or or_2 (nMOE, nOE, and_1_out);
  or or_3 (nMWE, nWE, and_1_out);
endmodule

module reg_pc_mux (
  input  PC,
  input  UWE,
  input  HR,
  input  WE,
  output H,
  output L
);

  wire and_1_out, nor_1_out, not_1_out, not_2_out, not_3_out;

  not not_1 (not_1_out, PC);
  nor nor_1 (nor_1_out, UWE, HR);
  not not_2 (not_2_out, PC);
  not not_3 (not_3_out, UWE);
  and and_1 (and_1_out, not_3_out, HR);
  or or_1 (H, not_1_out, nor_1_out, WE);
  or or_2 (L, not_2_out, WE, and_1_out);
endmodule

module fsm_main (
  input  nRESET,
  input  [4:0] OPCODE,
  input  COND,
  input  IRQ,
  input  CLK,
  output [2:0] CTR,
  output [2:0] STATE,
  output nIRQR
);

  wire fsm_has_next_1_n, fsm_machine_1_nmr, fsm_machine_1_pc, fsm_skip_jump_1_k;
  wire [2:0] fsm_machine_1_ns;

  fsm_skip_jump fsm_skip_jump_1 (.OPCODE(OPCODE), .COND(COND), .K(fsm_skip_jump_1_k));
  fsm_machine fsm_machine_1 (
    .nR(nRESET), .NS(fsm_machine_1_ns), .K(fsm_skip_jump_1_k), .N(fsm_has_next_1_n), .I(IRQ),
    .nMR(fsm_machine_1_nmr), .PC(fsm_machine_1_pc), .nRI(nIRQR), .S(STATE));
  fsm_state fsm_state_1 (.NS(fsm_machine_1_ns), .CLK(CLK), .S(STATE));
  fsm_counter fsm_counter_1 (.nMR(fsm_machine_1_nmr), .CE(fsm_machine_1_pc), .CLK(CLK), .CTR(CTR));
  fsm_has_next fsm_has_next_1 (.OPCODE(OPCODE), .S(STATE), .CTR(CTR), .N(fsm_has_next_1_n));
endmodule

module fsm_state (
  input  [2:0] NS,
  input  CLK,
  output [2:0] S
);

  _74273___8_bit_register_with_reset u_74273_8_bit_register_with_reset_1 (
    .nMR(1'b1), .Q0(S[0]), .D0(NS[0]), .D1(NS[1]), .Q1(S[1]), .Q2(S[2]), .D2(NS[2]), .CLK(CLK));  // open: D3, Q3, GND, VCC, Q7, D7, D6, Q6, Q5, D5, D4, Q4
endmodule

module fsm_counter (
  input  nMR,
  input  CE,
  input  CLK,
  output [2:0] CTR
);

  _74163___4_bit_sync_counter u_74163_4_bit_sync_counter_1 (
    .nMR(nMR), .CLK(CLK), .D0(1'b0), .D1(1'b0), .D2(1'b0), .D3(1'b0), .CEP(CE), .Q0(CTR[0]), .Q1(CTR[1]),
    .Q2(CTR[2]), .CET(1'b1), .nPE(1'b1));  // open: GND, VCC, TC, Q3
endmodule

module fsm_skip_jump (
  input  [4:0] OPCODE,
  input  COND,
  output K
);

  and and_1 (K, OPCODE[3], OPCODE[4], ~COND);  // AND_Gate
endmodule

module fsm_has_next (
  input  [4:0] OPCODE,
  input  [2:0] S,
  input  [2:0] CTR,
  output N
);

  wire and_1_out, and_2_out, and_3_out, and_4_out, and_5_out, fsm_has_next_byte_1_k, fsm_has_next_cycle_1_k,
       nand_1_out, nor_1_out;

  and and_1 (and_1_out, S[0], ~S[1], S[2]);  // AND_Gate
  fsm_has_next_byte fsm_has_next_byte_1 (
    .O4(OPCODE[4]), .O3(OPCODE[3]), .O2(OPCODE[2]), .O1(OPCODE[1]), .O0(OPCODE[0]), .C1(CTR[1]), .C0(CTR[0]),
    .K(fsm_has_next_byte_1_k));
  and and_2 (and_2_out, S[2], S[1], ~S[0]);  // AND_Gate
  nand nand_1 (nand_1_out, CTR[2], CTR[1]);
  nor nor_1 (nor_1_out, S[0], S[1], S[2]);
  fsm_has_next_cycle fsm_has_next_cycle_1 (
    .O4(OPCODE[4]), .O3(OPCODE[3]), .O2(OPCODE[2]), .O1(OPCODE[1]), .O0(OPCODE[0]), .S2(CTR[2]), .S1(CTR[1]),
    .S0(CTR[0]), .K(fsm_has_next_cycle_1_k));
  and and_3 (and_3_out, and_2_out, nand_1_out);
  and and_4 (and_4_out, and_1_out, ~fsm_has_next_byte_1_k);  // AND_Gate
  and and_5 (and_5_out, nor_1_out, ~fsm_has_next_cycle_1_k);  // AND_Gate
  or or_1 (N, and_4_out, and_3_out, and_5_out);

  // Notes on the sheet:
  //   NEXT CYCLE
  //   INTERRUPT CYCLES
endmodule

module fsm_has_next_byte (
  input  O4,
  input  O3,
  input  O2,
  input  O1,
  input  O0,
  input  C1,
  input  C0,
  output K
);

  wire and_1_out, and_2_out, and_3_out, and_4_out, and_5_out, and_6_out, and_7_out, and_8_out, and_9_out,
       and_10_out, and_11_out, and_12_out, and_13_out, not_1_out, not_2_out, not_3_out, not_4_out, not_5_out,
       not_6_out, not_7_out, not_8_out, not_9_out, not_10_out, not_11_out, not_12_out, not_13_out,
       not_14_out, not_15_out, not_16_out, not_17_out, not_18_out, not_19_out, not_20_out;

  not not_1 (not_1_out, O4);
  not not_2 (not_2_out, O2);
  not not_3 (not_3_out, O3);
  not not_4 (not_4_out, O2);
  not not_5 (not_5_out, O1);
  not not_6 (not_6_out, O0);
  not not_7 (not_7_out, O4);
  not not_8 (not_8_out, O3);
  not not_9 (not_9_out, O1);
  not not_10 (not_10_out, O1);
  not not_11 (not_11_out, O4);
  not not_12 (not_12_out, O3);
  not not_13 (not_13_out, O2);
  not not_14 (not_14_out, O4);
  not not_15 (not_15_out, O1);
  not not_16 (not_16_out, O0);
  not not_17 (not_17_out, O2);
  not not_18 (not_18_out, O3);
  not not_19 (not_19_out, O1);
  not not_20 (not_20_out, O1);
  and and_1 (and_1_out, not_1_out, not_2_out);
  and and_2 (and_2_out, not_3_out, not_4_out, not_5_out, not_6_out, C0);
  and and_3 (and_3_out, not_7_out, not_8_out, not_9_out, C1);
  and and_4 (and_4_out, C1, C0);
  and and_5 (and_5_out, not_10_out, O0, C1);
  and and_6 (and_6_out, not_11_out, O1, O0);
  and and_7 (and_7_out, not_12_out, not_13_out, O1, O0);
  and and_8 (and_8_out, not_14_out, O3, not_15_out, not_16_out, C0);
  and and_9 (and_9_out, O3, not_17_out, O1, C0);
  and and_10 (and_10_out, O4, not_18_out, O1, C1);
  and and_11 (and_11_out, O4, O2, C1);
  and and_12 (and_12_out, O4, O3, not_19_out, C1);
  and and_13 (and_13_out, O4, O3, O2, not_20_out);
  or or_1 (K, and_1_out, and_2_out, and_3_out, and_4_out, and_5_out, and_6_out, and_7_out, and_8_out, and_9_out, and_10_out, and_11_out, and_12_out, and_13_out);
endmodule

module fsm_has_next_cycle (
  input  O4,
  input  O3,
  input  O2,
  input  O1,
  input  O0,
  input  S2,
  input  S1,
  input  S0,
  output K
);

  wire and_1_out, and_2_out, and_3_out, and_4_out, and_5_out, and_6_out, and_7_out, and_8_out, and_9_out,
       and_10_out, and_11_out, and_12_out, and_13_out, and_14_out, and_15_out, and_16_out, not_1_out,
       not_2_out, not_3_out, not_4_out, not_5_out, not_6_out, not_7_out, not_8_out, not_9_out, not_10_out,
       not_11_out, not_12_out, not_13_out, not_14_out, not_15_out, not_16_out, not_17_out, not_18_out,
       not_19_out, not_20_out, not_21_out, not_22_out, not_23_out, not_24_out, not_25_out, not_26_out;

  not not_1 (not_1_out, O3);
  not not_2 (not_2_out, O2);
  not not_3 (not_3_out, O0);
  not not_4 (not_4_out, O2);
  not not_5 (not_5_out, O1);
  not not_6 (not_6_out, O0);
  not not_7 (not_7_out, O3);
  not not_8 (not_8_out, O1);
  not not_9 (not_9_out, O4);
  not not_10 (not_10_out, O2);
  not not_11 (not_11_out, O4);
  not not_12 (not_12_out, O3);
  not not_13 (not_13_out, O4);
  not not_14 (not_14_out, O3);
  not not_15 (not_15_out, O4);
  not not_16 (not_16_out, O0);
  not not_17 (not_17_out, O3);
  not not_18 (not_18_out, O2);
  not not_19 (not_19_out, O4);
  not not_20 (not_20_out, O4);
  not not_21 (not_21_out, O4);
  not not_22 (not_22_out, O1);
  not not_23 (not_23_out, O2);
  not not_24 (not_24_out, O1);
  not not_25 (not_25_out, O1);
  not not_26 (not_26_out, O2);
  and and_1 (and_1_out, not_1_out, not_2_out, not_3_out);
  and and_2 (and_2_out, not_4_out, not_5_out, not_6_out);
  and and_3 (and_3_out, not_7_out, not_8_out, S0);
  and and_4 (and_4_out, not_9_out, not_10_out, S2, S1);
  and and_5 (and_5_out, not_11_out, not_12_out, O0, S2);
  and and_6 (and_6_out, not_13_out, not_14_out, O1);
  and and_7 (and_7_out, not_15_out, O1, not_16_out);
  and and_8 (and_8_out, not_17_out, O1, S1);
  and and_9 (and_9_out, not_18_out, O1, S1, S0);
  and and_10 (and_10_out, not_19_out, O1, S2, S0);
  and and_11 (and_11_out, not_20_out, O2, S0);
  and and_12 (and_12_out, not_21_out, O2, not_22_out, O0);
  and and_13 (and_13_out, O4, not_23_out, not_24_out);
  and and_14 (and_14_out, O4, not_25_out, S1, S0);
  and and_15 (and_15_out, O4, O2, O1, S2, S1);
  and and_16 (and_16_out, O4, O3, not_26_out, S0);
  or or_1 (K, and_1_out, and_2_out, and_3_out, and_4_out, and_5_out, and_6_out, and_7_out, and_8_out, and_9_out, and_10_out, and_11_out, and_12_out, and_13_out, and_14_out, and_15_out, and_16_out);
endmodule

module fsm_machine (
  input  nR,
  input  [2:0] S,
  input  K,
  input  N,
  input  I,
  output [2:0] NS,
  output nMR,
  output PC,
  output nRI
);

  wire and_1_out, and_2_out, and_3_out, and_4_out, and_5_out, and_6_out, and_7_out, and_8_out, and_9_out,
       and_10_out, and_11_out, and_12_out, and_13_out, and_14_out, and_15_out, and_16_out, not_1_out,
       not_2_out, not_3_out, not_4_out, not_5_out, not_6_out, not_7_out, not_8_out, not_9_out, not_10_out,
       not_11_out, not_12_out, not_13_out, not_14_out, not_15_out, not_16_out, not_17_out, not_18_out,
       not_19_out, not_20_out;

  not not_1 (not_1_out, S[0]);
  not not_2 (not_2_out, N);
  not not_3 (not_3_out, S[1]);
  not not_4 (not_4_out, N);
  not not_5 (not_5_out, S[1]);
  not not_6 (not_6_out, S[0]);
  not not_7 (not_7_out, S[1]);
  not not_8 (not_8_out, S[0]);
  not not_9 (not_9_out, S[1]);
  not not_10 (not_10_out, S[0]);
  not not_11 (not_11_out, S[1]);
  not not_12 (not_12_out, nR);
  and and_1 (and_1_out, not_1_out, not_2_out);
  and and_2 (and_2_out, S[2], N);
  and and_3 (and_3_out, S[2], K);
  not not_13 (not_13_out, nR);
  not not_14 (not_14_out, S[2]);
  and and_4 (and_4_out, not_14_out, not_15_out, I);
  not not_15 (not_15_out, N);
  and and_5 (and_5_out, not_3_out, S[0], K, not_4_out, I);
  and and_6 (and_6_out, S[1], not_16_out, N);
  not not_16 (not_16_out, S[0]);
  not not_17 (not_17_out, nR);
  and and_7 (and_7_out, S[2], not_5_out, not_6_out);
  and and_8 (and_8_out, nR, not_18_out, N);
  not not_18 (not_18_out, S[1]);
  and and_9 (and_9_out, nR, not_19_out, N);
  not not_19 (not_19_out, S[0]);
  and and_10 (and_10_out, nR, S[2], not_7_out, not_8_out);
  and and_11 (and_11_out, nR, not_20_out, N);
  not not_20 (not_20_out, S[2]);
  and and_12 (and_12_out, nR, not_9_out, S[0], N);
  and and_13 (and_13_out, nR, S[1], not_10_out, N);
  and and_14 (and_14_out, nR, not_11_out);
  and and_15 (and_15_out, nR, N);
  and and_16 (and_16_out, nR, S[0]);
  or or_1 (NS[2], not_12_out, and_1_out, S[1], and_2_out, and_3_out);
  or or_2 (NS[1], not_13_out, and_4_out, and_5_out, and_6_out);
  or or_3 (NS[0], not_17_out, and_7_out);
  or or_4 (nMR, and_8_out, and_9_out, and_10_out);
  or or_5 (PC, and_11_out, and_12_out, and_13_out);
  or or_6 (nRI, and_14_out, and_15_out, and_16_out);
endmodule

module alu_temp_dec (
  input  T,
  input  M,
  input  O1,
  input  O0,
  input  X,
  output A,
  output M2,
  output S3,
  output S2,
  output S1,
  output S0,
  output E,
  output C,
  output N,
  output F,
  output ZE,
  output AE
);

  wire and_1_out, and_2_out, and_3_out, and_4_out, and_5_out, and_6_out, and_7_out, and_8_out, and_9_out,
       and_10_out, and_11_out, and_12_out, and_13_out, and_14_out, and_15_out, and_16_out, and_17_out,
       and_18_out, and_19_out, and_20_out, and_21_out, and_22_out, and_23_out, and_24_out, and_25_out,
       and_26_out, and_27_out, and_28_out, and_29_out, and_31_out, not_1_out, not_2_out, not_3_out,
       not_4_out, not_5_out, not_6_out, or_1_out, or_2_out, or_3_out, or_4_out, xor_1_out;

  not not_1 (not_1_out, T);
  not not_2 (not_2_out, M);
  not not_3 (not_3_out, O1);
  not not_4 (not_4_out, O0);
  not not_5 (not_5_out, X);
  and and_1 (and_1_out, not_1_out, not_2_out);
  and and_2 (and_2_out, O1, not_4_out);
  and and_3 (and_3_out, M, not_4_out, not_5_out);
  and and_4 (and_4_out, T, not_3_out);
  and and_5 (and_5_out, not_3_out, O0);
  or or_1 (or_1_out, not_1_out, M);
  and and_6 (and_6_out, M, X);
  and and_7 (and_7_out, not_1_out, and_9_out);
  and and_8 (and_8_out, M, O0);
  and and_9 (and_9_out, M, O1);
  and and_10 (and_10_out, not_3_out, and_1_out);
  or or_2 (or_2_out, and_1_out, not_3_out);
  and and_11 (and_11_out, and_5_out, or_1_out);
  or or_3 (or_3_out, and_6_out, T);
  and and_12 (and_12_out, or_3_out, and_2_out);
  and and_13 (and_13_out, T, xor_1_out);
  xor xor_1 (xor_1_out, M, O1);
  and and_14 (and_14_out, or_2_out, O0);
  and and_15 (and_15_out, O1, not_4_out);
  not not_6 (not_6_out, or_1_out);
  and and_16 (and_16_out, not_1_out, or_4_out);
  or or_4 (or_4_out, not_5_out, and_15_out);
  or or_5 (A, not_2_out, not_3_out, T);
  and and_17 (and_17_out, and_1_out, not_4_out);
  and and_18 (and_18_out, O1, and_8_out);
  and and_19 (and_19_out, T, M);
  and and_20 (and_20_out, not_6_out, O1);
  and and_21 (and_21_out, not_3_out, and_8_out);
  and and_22 (and_22_out, not_2_out, not_3_out);
  and and_23 (and_23_out, not_1_out, O0);
  and and_24 (and_24_out, and_4_out, not_4_out);
  and and_25 (and_25_out, and_1_out, O1, O0);
  and and_26 (and_26_out, not_1_out, X);
  and and_27 (and_27_out, T, not_4_out);
  and and_28 (and_28_out, not_1_out, O0);
  and and_29 (and_29_out, T, not_3_out);
  and and_30 (F, not_1_out, M, not_3_out, not_5_out);
  and and_31 (and_31_out, and_3_out, not_1_out);
  or or_6 (M2, and_10_out, and_17_out, and_18_out, and_19_out);
  or or_7 (S3, and_16_out, and_14_out, and_4_out);
  or or_8 (S2, and_11_out, and_12_out, and_20_out);
  or or_9 (S1, and_10_out, and_2_out, and_21_out, and_7_out, and_13_out);
  or or_10 (S0, and_22_out, and_23_out, and_7_out, and_24_out);
  or or_11 (E, X, and_25_out);
  or or_12 (C, and_26_out, and_8_out, and_9_out, and_27_out);
  or or_13 (N, and_28_out, and_9_out, and_29_out);
  or or_14 (ZE, and_3_out, and_9_out, T);
  or or_15 (AE, and_31_out, and_7_out, not_6_out);
endmodule

module tests (
);

  wire clock_1_out, comparator_1_eq, counter_1_carry, not_1_out, not_2_out;
  wire [4:0] counter_1_q;
  wire [11:0] alu_decoder_1_a, alu_temp_dec_1_a;

  Clock clock_1 (.out(clock_1_out));
  Counter #(.width(5), .max('h1f)) counter_1 (
    .count(1'b1), .Q(counter_1_q), .carry(counter_1_carry), .clk(clock_1_out));  // open: load, D, clr
  alu_temp_dec alu_temp_dec_1 (
    .T(counter_1_q[0]), .M(counter_1_q[1]), .O1(counter_1_q[2]), .O0(counter_1_q[3]), .X(counter_1_q[4]),
    .A(alu_temp_dec_1_a[0]), .M2(alu_temp_dec_1_a[1]), .S3(alu_temp_dec_1_a[2]), .S2(alu_temp_dec_1_a[3]),
    .S1(alu_temp_dec_1_a[4]), .S0(alu_temp_dec_1_a[5]), .E(alu_temp_dec_1_a[6]), .C(alu_temp_dec_1_a[7]),
    .N(alu_temp_dec_1_a[8]), .F(alu_temp_dec_1_a[9]), .ZE(alu_temp_dec_1_a[10]), .AE(alu_temp_dec_1_a[11]));
  alu_decoder alu_decoder_1 (
    .T(counter_1_q[0]), .A(alu_decoder_1_a[0]), .M(counter_1_q[1]), .O1(counter_1_q[2]), .O0(counter_1_q[3]),
    .M2(alu_decoder_1_a[1]), .X(counter_1_q[4]), .S3(alu_decoder_1_a[2]), .S2(alu_decoder_1_a[3]),
    .S1(alu_decoder_1_a[4]), .S0(alu_decoder_1_a[5]), .E(alu_decoder_1_a[6]), .C(alu_decoder_1_a[7]),
    .N(alu_decoder_1_a[8]), .F(alu_decoder_1_a[9]), .ZE(alu_decoder_1_a[10]), .AE(alu_decoder_1_a[11]));
  Comparator #(.width(12), .mode("unsigned")) comparator_1 (
    .a(alu_temp_dec_1_a), .b(alu_decoder_1_a), .eq(comparator_1_eq));  // open: gt, lt
  not not_1 (not_1_out, comparator_1_eq);
  Counter counter_2 (.count(not_1_out), .clk(not_2_out));  // open: load, D, Q, carry, clr
  not not_2 (not_2_out, clock_1_out);
endmodule
